// Logisim project 16bitcomputer.circ as structural Verilog
module main (
  input  [15:0] in_1,
  input  [15:0] in_2,
  output [31:0] out_3
);

  Bit16_Multiplier bit16_multiplier_1 (
    .Bit16_B(in_1), .Bit16_A(in_2), .Lower_Word(out_3[15:0]), .Upper_Word(out_3[31:16]));
endmodule

module Bit16_Add (
  input  FP_Op,
  input  Carry_In,
  input  [15:0] Bit16_A,
  input  [15:0] Bit16_B,
  output [15:0] Bit16_Result,
  output Carry_Out
);

  wire and_1_out, and_2_out, and_3_out, and_4_out, and_5_out, and_6_out, and_7_out, and_8_out, and_9_out,
       and_10_out, and_11_out, and_12_out, and_13_out, and_14_out, and_15_out, and_16_out, and_17_out,
       bit4_cla_logic_1_c2, bit4_cla_logic_1_c3, bit4_cla_logic_1_c4, bit4_cla_logic_1_cout,
       bit4_cla_logic_1_pg, bit4_cla_logic_2_c2, bit4_cla_logic_2_c3, bit4_cla_logic_2_c4,
       bit4_cla_logic_2_cout, bit4_cla_logic_2_pg, bit4_cla_logic_3_c2, bit4_cla_logic_3_c3,
       bit4_cla_logic_3_c4, bit4_cla_logic_3_cout, bit4_cla_logic_3_pg, bit4_cla_logic_4_c2,
       bit4_cla_logic_4_c3, bit4_cla_logic_4_c4, bit4_cla_logic_4_cout, bit4_cla_logic_4_pg,
       bit4_cla_logic_5_c2, bit4_cla_logic_5_c3, bit4_cla_logic_5_c4, bit4_cla_logic_5_cout, xor_1_out,
       xor_2_out, xor_3_out, xor_4_out, xor_5_out, xor_6_out, xor_7_out, xor_8_out, xor_9_out, xor_10_out,
       xor_11_out, xor_12_out, xor_13_out, xor_14_out, xor_15_out, xor_16_out;

  xor xor_1 (xor_1_out, Bit16_A[0], Bit16_B[0]);
  and and_1 (and_1_out, Bit16_B[0], Bit16_A[0]);
  xor xor_2 (xor_2_out, Bit16_A[1], Bit16_B[1]);
  and and_2 (and_2_out, Bit16_B[1], Bit16_A[1]);
  xor xor_3 (xor_3_out, Bit16_A[2], Bit16_B[2]);
  and and_3 (and_3_out, Bit16_B[2], Bit16_A[2]);
  xor xor_4 (xor_4_out, Bit16_A[3], Bit16_B[3]);
  and and_4 (and_4_out, Bit16_B[3], Bit16_A[3]);
  xor xor_5 (xor_5_out, Bit16_A[4], Bit16_B[4]);
  and and_5 (and_5_out, Bit16_B[4], Bit16_A[4]);
  xor xor_6 (xor_6_out, Bit16_A[5], Bit16_B[5]);
  and and_6 (and_6_out, Bit16_B[5], Bit16_A[5]);
  xor xor_7 (xor_7_out, Bit16_A[6], Bit16_B[6]);
  and and_7 (and_7_out, Bit16_B[6], Bit16_A[6]);
  xor xor_8 (xor_8_out, Bit16_A[7], Bit16_B[7]);
  and and_8 (and_8_out, Bit16_B[7], Bit16_A[7]);
  xor xor_9 (xor_9_out, Bit16_A[8], Bit16_B[8]);
  and and_9 (and_9_out, Bit16_B[8], Bit16_A[8]);
  xor xor_10 (xor_10_out, Bit16_A[9], Bit16_B[9]);
  and and_10 (and_10_out, Bit16_B[9], Bit16_A[9]);
  xor xor_11 (xor_11_out, Bit16_A[10], Bit16_B[10]);
  and and_11 (and_11_out, Bit16_B[10], Bit16_A[10]);
  xor xor_12 (xor_12_out, Bit16_A[11], Bit16_B[11]);
  and and_12 (and_12_out, Bit16_B[11], Bit16_A[11]);
  xor xor_13 (xor_13_out, Bit16_A[12], Bit16_B[12]);
  and and_13 (and_13_out, Bit16_B[12], Bit16_A[12]);
  xor xor_14 (xor_14_out, Bit16_A[13], Bit16_B[13]);
  and and_14 (and_14_out, Bit16_B[13], Bit16_A[13]);
  xor xor_15 (xor_15_out, Bit16_A[14], Bit16_B[14]);
  and and_15 (and_15_out, Bit16_B[14], Bit16_A[14]);
  xor xor_16 (xor_16_out, Bit16_A[15], Bit16_B[15]);
  and and_16 (and_16_out, Bit16_B[15], Bit16_A[15]);
  xor xor_17 (Bit16_Result[0], Carry_In, xor_1_out);
  xor xor_18 (Bit16_Result[1], bit4_cla_logic_1_c2, xor_2_out);
  xor xor_19 (Bit16_Result[2], bit4_cla_logic_1_c3, xor_3_out);
  xor xor_20 (Bit16_Result[3], bit4_cla_logic_1_c4, xor_4_out);
  xor xor_21 (Bit16_Result[4], bit4_cla_logic_5_c2, xor_5_out);
  xor xor_22 (Bit16_Result[5], bit4_cla_logic_2_c2, xor_6_out);
  xor xor_23 (Bit16_Result[6], bit4_cla_logic_2_c3, xor_7_out);
  xor xor_24 (Bit16_Result[7], bit4_cla_logic_2_c4, xor_8_out);
  xor xor_25 (Bit16_Result[8], bit4_cla_logic_5_c3, xor_9_out);
  xor xor_26 (Bit16_Result[9], bit4_cla_logic_3_c2, xor_10_out);
  xor xor_27 (Bit16_Result[10], bit4_cla_logic_3_c3, xor_11_out);
  xor xor_28 (Bit16_Result[11], bit4_cla_logic_3_c4, xor_12_out);
  xor xor_29 (Bit16_Result[12], bit4_cla_logic_5_c4, xor_13_out);
  xor xor_30 (Bit16_Result[13], bit4_cla_logic_4_c2, xor_14_out);
  xor xor_31 (Bit16_Result[14], bit4_cla_logic_4_c3, xor_15_out);
  xor xor_32 (Bit16_Result[15], bit4_cla_logic_4_c4, xor_16_out);
  Bit4_CLA_Logic bit4_cla_logic_1 (
    .Cin(Carry_In), .P1(xor_1_out), .G1(and_1_out), .P2(xor_2_out), .G2(and_2_out), .P3(xor_3_out),
    .G3(and_3_out), .P4(xor_4_out), .G4(and_4_out), .C2(bit4_cla_logic_1_c2), .C3(bit4_cla_logic_1_c3),
    .C4(bit4_cla_logic_1_c4), .COUT(bit4_cla_logic_1_cout), .PG(bit4_cla_logic_1_pg));
  Bit4_CLA_Logic bit4_cla_logic_2 (
    .Cin(bit4_cla_logic_5_c2), .P1(xor_5_out), .G1(and_5_out), .P2(xor_6_out), .G2(and_6_out),
    .P3(xor_7_out), .G3(and_7_out), .P4(xor_8_out), .G4(and_8_out), .C2(bit4_cla_logic_2_c2),
    .C3(bit4_cla_logic_2_c3), .C4(bit4_cla_logic_2_c4), .COUT(bit4_cla_logic_2_cout), .PG(bit4_cla_logic_2_pg));
  Bit4_CLA_Logic bit4_cla_logic_3 (
    .Cin(bit4_cla_logic_5_c3), .P1(xor_9_out), .G1(and_9_out), .P2(xor_10_out), .G2(and_10_out),
    .P3(xor_11_out), .G3(and_11_out), .P4(xor_12_out), .G4(and_12_out), .C2(bit4_cla_logic_3_c2),
    .C3(bit4_cla_logic_3_c3), .C4(bit4_cla_logic_3_c4), .COUT(bit4_cla_logic_3_cout), .PG(bit4_cla_logic_3_pg));
  Bit4_CLA_Logic bit4_cla_logic_4 (
    .Cin(bit4_cla_logic_5_c4), .P1(xor_13_out), .G1(and_13_out), .P2(xor_14_out), .G2(and_14_out),
    .P3(xor_15_out), .G3(and_15_out), .P4(xor_16_out), .G4(and_16_out), .C2(bit4_cla_logic_4_c2),
    .C3(bit4_cla_logic_4_c3), .C4(bit4_cla_logic_4_c4), .COUT(bit4_cla_logic_4_cout), .PG(bit4_cla_logic_4_pg));
  Bit4_CLA_Logic bit4_cla_logic_5 (
    .Cin(Carry_In), .P1(bit4_cla_logic_1_pg), .G1(bit4_cla_logic_1_cout), .P2(bit4_cla_logic_2_pg),
    .G2(bit4_cla_logic_2_cout), .P3(bit4_cla_logic_3_pg), .G3(bit4_cla_logic_3_cout),
    .P4(bit4_cla_logic_4_pg), .G4(bit4_cla_logic_4_cout), .C2(bit4_cla_logic_5_c2), .C3(bit4_cla_logic_5_c3),
    .C4(bit4_cla_logic_5_c4), .COUT(bit4_cla_logic_5_cout));  // open: PG
  and and_17 (and_17_out, Bit16_Result[11], FP_Op);
  or or_1 (Carry_Out, bit4_cla_logic_5_cout, and_17_out);
endmodule

module Bit16_ALU (
  input  in_1,
  input  in_2,
  input  Clock,
  input  [4:0] Bit5_Opcode,
  input  Signed_Integer_Operation,
  input  [15:0] Bit16_A,
  input  [15:0] Bit16_B,
  input  in_8,
  output CPU_WAIT_FOR_ALU_OP,
  output Carry,
  output Borrow,
  output Negative,
  output Overflow,
  output Zero,
  output [15:0] Bit16_Result
);

  wire and_1_out, and_2_out, and_3_out, and_4_out, and_5_out, and_6_out, and_7_out, and_8_out, and_9_out,
       and_10_out, and_11_out, and_12_out, and_13_out, and_15_out, and_16_out, and_17_out, and_18_out,
       and_19_out, and_20_out, and_21_out, and_22_out, and_23_out, and_24_out, bit16_add_1_carry_out,
       d_ff_2_qn, d_ff_3_qn, d_ff_4_qn, d_ff_5_qn, demultiplexer_1_out2, demultiplexer_1_out4,
       demultiplexer_1_out8, demultiplexer_1_out9, demultiplexer_1_out11, demultiplexer_2_out0,
       demultiplexer_2_out1, demultiplexer_2_out2, demultiplexer_2_out3, demultiplexer_2_out4,
       demultiplexer_2_out5, demultiplexer_2_out6, demultiplexer_2_out7, demultiplexer_2_out8,
       demultiplexer_2_out9, demultiplexer_2_out10, demultiplexer_2_out11, demultiplexer_2_out12,
       demultiplexer_2_out13, demultiplexer_2_out14, demultiplexer_2_out15, demultiplexer_3_out0,
       demultiplexer_3_out1, demultiplexer_3_out2, demultiplexer_3_out3, demultiplexer_3_out4,
       demultiplexer_3_out5, demultiplexer_3_out6, demultiplexer_3_out7, demultiplexer_3_out8,
       demultiplexer_3_out9, demultiplexer_3_out10, demultiplexer_3_out11, demultiplexer_3_out12,
       demultiplexer_3_out13, demultiplexer_3_out14, demultiplexer_3_out15, nor_1_out, nor_2_out, not_1_out,
       not_2_out, not_3_out, not_4_out, not_5_out, or_1_out, or_2_out, or_3_out, or_4_out, or_5_out, or_8_out;
  wire [0:0] or_9_out;
  wire [3:0] bit4_adder_1_bit4_result, bit4_controlled_buffer_1_bit4_out, bit4_controlled_buffer_2_bit4_out,
       bit4_twos_complementer_1_bit4_result, bit4_twos_complementer_2_bit4_result, d_ff_2_q;
  wire [4:0] bit5_twos_complementer_1_bit5_result;
  wire [9:0] bit16_add_1_bit16_result_2;
  wire [15:0] bit16_controlled_buffer_1_bit16_out, bit16_controlled_buffer_2_bit16_out,
       bit16_controlled_buffer_3_bit16_out, bit16_controlled_buffer_4_bit16_out,
       bit16_controlled_buffer_5_bit16_out, bit16_controlled_buffer_6_bit16_out,
       bit16_left_shift_1_bit16_result, bit16_multiplier_1_lower_word, bit16_multiplier_1_upper_word,
       bit16_right_shift_1_bit16_result, or_6_out, or_7_out, or_10_out, register_1_q, s_r_ff_16_q,
       twos_complementer_1_bit16_result, twos_complementer_2_bit16_result, twos_complementer_3_bit16_result,
       twos_complementer_4_bit16_result, undriven;
  wire [15:10] bit16_add_1_bit16_result;

  // Probe on Bit16_B[13:10]
  Bit5_Twos_Complementer bit5_twos_complementer_1 (.Bit5_Result(bit5_twos_complementer_1_bit5_result));  // open: Bit5_In
  Bit4_Twos_Complementer bit4_twos_complementer_1 (
    .Bit4_In(Bit16_B[13:10]), .Bit4_Result(bit4_twos_complementer_1_bit4_result));
  Bit5_Adder bit5_adder_1 (.Bit5_B(bit5_twos_complementer_1_bit5_result));  // open: Cin, Bit5_A, Bit5_Result, Cout
  Bit4_Adder bit4_adder_1 (
    .Cin(1'b1), .Bit4_A(Bit16_A[13:10]), .Bit4_B(bit4_twos_complementer_1_bit4_result),
    .Bit4_Result(bit4_adder_1_bit4_result));  // open: Cout
  // Probe on bit4_adder_1_bit4_result
  and and_1 (and_1_out, Bit16_B[14], ~or_1_out);  // AND_Gate
  D_Flip_Flop #(.trigger("falling")) d_ff_1 (.clk(in_1));  // open: D, Q, Qn, preset, reset
  not not_1 (not_1_out, Bit5_Opcode[4]);
  // Probe on Bit16_A
  // Probe on Bit16_B
  and and_2 (and_2_out, or_1_out, Bit16_B[14]);
  // Probe on {in_8, Bit16_A[14:10], bit16_add_1_bit16_result_2}
  Demultiplexer #(.select(4)) demultiplexer_1 (
    .out2(demultiplexer_1_out2), .out4(demultiplexer_1_out4), .out8(demultiplexer_1_out8),
    .out9(demultiplexer_1_out9), .out11(demultiplexer_1_out11), .in(not_1_out), .sel(Bit5_Opcode[3:0]));  // open: out0, out1, out3, out5, out6, out7, out10, out12, out13, out14, out15
  Bit4_Twos_Complementer bit4_twos_complementer_2 (
    .Bit4_In(bit4_adder_1_bit4_result), .Bit4_Result(bit4_twos_complementer_2_bit4_result));
  and and_3 (and_3_out, ~Bit5_Opcode[2], Bit5_Opcode[3], not_1_out);  // AND_Gate
  and and_4 (and_4_out, Bit5_Opcode[3], not_1_out, ~Bit5_Opcode[2], or_3_out);  // AND_Gate
  or or_1 (or_1_out, demultiplexer_1_out8, demultiplexer_1_out9);
  or or_2 (or_2_out, demultiplexer_1_out9, demultiplexer_1_out2, or_3_out);
  Bit4_Controlled_Buffer bit4_controlled_buffer_1 (
    .Bit4_In(bit4_twos_complementer_2_bit4_result), .Enable(and_1_out),
    .Bit4_Out(bit4_controlled_buffer_1_bit4_out));
  Bit4_Controlled_Buffer bit4_controlled_buffer_2 (
    .Bit4_In(bit4_adder_1_bit4_result), .Enable(and_2_out), .Bit4_Out(bit4_controlled_buffer_2_bit4_out));
  or or_3 (or_3_out, demultiplexer_1_out4, demultiplexer_1_out11);
  // Probe on twos_complementer_2_bit16_result
  and and_5 (and_5_out, bit16_add_1_carry_out, or_3_out);
  or or_4 (or_4_out, and_4_out, and_3_out, Signed_Integer_Operation);
  or or_5 (or_5_out, demultiplexer_1_out9, and_4_out, Signed_Integer_Operation, demultiplexer_1_out8);
  // Probe on bit4_controlled_buffer_2_bit4_out
  // Probe on bit4_controlled_buffer_1_bit4_out
  Demultiplexer #(.select(4)) demultiplexer_2 (
    .out0(demultiplexer_2_out0), .out1(demultiplexer_2_out1), .out2(demultiplexer_2_out2),
    .out3(demultiplexer_2_out3), .out4(demultiplexer_2_out4), .out5(demultiplexer_2_out5),
    .out6(demultiplexer_2_out6), .out7(demultiplexer_2_out7), .out8(demultiplexer_2_out8),
    .out9(demultiplexer_2_out9), .out10(demultiplexer_2_out10), .out11(demultiplexer_2_out11),
    .out12(demultiplexer_2_out12), .out13(demultiplexer_2_out13), .out14(demultiplexer_2_out14),
    .out15(demultiplexer_2_out15), .in(and_5_out), .sel(d_ff_2_q));
  not not_2 (not_2_out, or_3_out);
  S_R_Flip_Flop s_r_ff_1 (
    .S(demultiplexer_2_out15), .R(in_2), .clk(and_6_out), .Q(s_r_ff_16_q[15]), .reset(not_3_out));  // open: Qn, preset
  not not_3 (not_3_out, or_3_out);
  S_R_Flip_Flop s_r_ff_2 (
    .S(demultiplexer_2_out14), .R(in_2), .clk(and_6_out), .Q(s_r_ff_16_q[14]), .reset(not_3_out));  // open: Qn, preset
  // Probe on d_ff_2_q
  nor nor_1 (nor_1_out, d_ff_2_q[0], d_ff_2_q[1], d_ff_2_q[2], d_ff_2_q[3], ~or_3_out);  // NOR_Gate
  D_Flip_Flop #(.trigger("falling")) d_ff_2 (
    .D(d_ff_2_qn), .clk(and_6_out), .Q(d_ff_2_q[0]), .Qn(d_ff_2_qn), .reset(not_3_out));  // open: preset
  and and_6 (and_6_out, or_3_out, Clock);
  Twos_Complementer twos_complementer_1 (
    .Floating_Point_Bit_Strip(and_3_out), .Cut_MSB(or_4_out), .Bit16_Input(Bit16_A),
    .Bit16_Result(twos_complementer_1_bit16_result));  // open: Allow_Twos_Complement
  Twos_Complementer twos_complementer_2 (
    .Floating_Point_Bit_Strip(and_3_out), .Cut_MSB(or_5_out), .Bit16_Input(Bit16_B),
    .Bit16_Result(twos_complementer_2_bit16_result));  // open: Allow_Twos_Complement
  // Probe on twos_complementer_3_bit16_result
  nor nor_2 (nor_2_out, and_1_out, and_2_out);
  Bit16_Left_Shift bit16_left_shift_1 (
    .Bit16_Data(twos_complementer_2_bit16_result), .Bit4_Shift(bit4_controlled_buffer_2_bit4_out),
    .Bit16_Result(bit16_left_shift_1_bit16_result));  // open: Shift_Overflow
  Bit16_Right_Shift bit16_right_shift_1 (
    .Bit16_Data(twos_complementer_2_bit16_result), .Bit4_Shift(bit4_controlled_buffer_1_bit4_out),
    .Bit16_Result(bit16_right_shift_1_bit16_result));  // open: Shift_Overflow
  S_R_Flip_Flop s_r_ff_3 (
    .S(demultiplexer_2_out13), .R(in_2), .clk(and_6_out), .Q(s_r_ff_16_q[13]), .reset(not_3_out));  // open: Qn, preset
  D_Flip_Flop #(.trigger("falling")) d_ff_3 (
    .D(d_ff_3_qn), .clk(d_ff_2_q[0]), .Q(d_ff_2_q[1]), .Qn(d_ff_3_qn), .reset(not_3_out));  // open: preset
  Bit16_Controlled_Buffer bit16_controlled_buffer_1 (
    .Enable(not_2_out), .Bit16_In(twos_complementer_1_bit16_result),
    .Bit16_Out(bit16_controlled_buffer_1_bit16_out));
  S_R_Flip_Flop s_r_ff_4 (
    .S(demultiplexer_2_out12), .R(in_2), .clk(and_6_out), .Q(s_r_ff_16_q[12]), .reset(not_3_out));  // open: Qn, preset
  D_Flip_Flop #(.trigger("falling")) d_ff_4 (
    .D(d_ff_4_qn), .clk(d_ff_2_q[1]), .Q(d_ff_2_q[2]), .Qn(d_ff_4_qn), .reset(not_3_out));  // open: preset
  assign or_6_out = register_1_q | bit16_controlled_buffer_1_bit16_out;  // OR_Gate or_6, 16 bits wide
  S_R_Flip_Flop s_r_ff_5 (
    .S(demultiplexer_2_out11), .R(in_2), .clk(and_6_out), .Q(s_r_ff_16_q[11]), .reset(not_3_out));  // open: Qn, preset
  Demultiplexer #(.select(4)) demultiplexer_3 (
    .out0(demultiplexer_3_out0), .out1(demultiplexer_3_out1), .out2(demultiplexer_3_out2),
    .out3(demultiplexer_3_out3), .out4(demultiplexer_3_out4), .out5(demultiplexer_3_out5),
    .out6(demultiplexer_3_out6), .out7(demultiplexer_3_out7), .out8(demultiplexer_3_out8),
    .out9(demultiplexer_3_out9), .out10(demultiplexer_3_out10), .out11(demultiplexer_3_out11),
    .out12(demultiplexer_3_out12), .out13(demultiplexer_3_out13), .out14(demultiplexer_3_out14),
    .out15(demultiplexer_3_out15), .in(or_3_out), .sel(d_ff_2_q));
  S_R_Flip_Flop s_r_ff_6 (
    .S(demultiplexer_2_out10), .R(in_2), .clk(and_6_out), .Q(s_r_ff_16_q[10]), .reset(not_3_out));  // open: Qn, preset
  D_Flip_Flop #(.trigger("falling")) d_ff_5 (
    .D(d_ff_5_qn), .clk(d_ff_2_q[2]), .Q(d_ff_2_q[3]), .Qn(d_ff_5_qn), .reset(not_3_out));  // open: preset
  not not_4 (not_4_out, or_3_out);
  Bit16_Add bit16_add_1 (
    .FP_Op(and_3_out), .Bit16_A(or_6_out), .Bit16_B(twos_complementer_3_bit16_result),
    .Bit16_Result({bit16_add_1_bit16_result, bit16_add_1_bit16_result_2}), .Carry_Out(bit16_add_1_carry_out));  // open: Carry_In
  Bit16_Multiplier bit16_multiplier_1 (
    .Bit16_B(twos_complementer_2_bit16_result), .Bit16_A(twos_complementer_1_bit16_result),
    .Lower_Word(bit16_multiplier_1_lower_word), .Upper_Word(bit16_multiplier_1_upper_word));
  Bit16_Controlled_Buffer bit16_controlled_buffer_2 (
    .Enable(nor_2_out), .Bit16_In(twos_complementer_2_bit16_result),
    .Bit16_Out(bit16_controlled_buffer_2_bit16_out));
  assign or_7_out = bit16_controlled_buffer_2_bit16_out | bit16_controlled_buffer_3_bit16_out | bit16_controlled_buffer_4_bit16_out;  // OR_Gate or_7, 16 bits wide
  Bit16_Controlled_Buffer bit16_controlled_buffer_3 (
    .Enable(and_2_out), .Bit16_In(bit16_left_shift_1_bit16_result),
    .Bit16_Out(bit16_controlled_buffer_3_bit16_out));
  Bit16_Controlled_Buffer bit16_controlled_buffer_4 (
    .Enable(and_1_out), .Bit16_In(bit16_right_shift_1_bit16_result),
    .Bit16_Out(bit16_controlled_buffer_4_bit16_out));
  and and_7 (and_7_out, demultiplexer_3_out15, twos_complementer_1_bit16_result[0]);
  and and_8 (and_8_out, demultiplexer_3_out14, twos_complementer_1_bit16_result[1]);
  and and_9 (and_9_out, demultiplexer_3_out13, twos_complementer_1_bit16_result[2]);
  and and_10 (and_10_out, d_ff_2_q[0], d_ff_2_q[1], d_ff_2_q[2], d_ff_2_q[3]);
  Register #(.trigger("falling"), .width(16)) register_1 (
    .D({or_10_out[14:0], or_9_out[0]}), .en(or_3_out), .clk(and_6_out), .Q(register_1_q), .clr(or_8_out));
  not not_5 (not_5_out, bit16_add_1_carry_out);
  S_R_Flip_Flop s_r_ff_7 (
    .S(demultiplexer_2_out9), .R(in_2), .clk(and_6_out), .Q(s_r_ff_16_q[9]), .reset(not_3_out));  // open: Qn, preset
  and and_11 (and_11_out, demultiplexer_3_out12, twos_complementer_1_bit16_result[3]);
  and and_12 (and_12_out, demultiplexer_3_out11, twos_complementer_1_bit16_result[4]);
  and and_13 (and_13_out, demultiplexer_3_out10, twos_complementer_1_bit16_result[5]);
  and and_14 (CPU_WAIT_FOR_ALU_OP, ~and_10_out, or_3_out);  // AND_Gate
  or or_8 (or_8_out, not_4_out, not_3_out);
  // Probe on {bit16_add_1_bit16_result, bit16_add_1_bit16_result_2}
  S_R_Flip_Flop s_r_ff_8 (
    .S(demultiplexer_2_out8), .R(in_2), .clk(and_6_out), .Q(s_r_ff_16_q[8]), .reset(not_3_out));  // open: Qn, preset
  and and_15 (and_15_out, demultiplexer_3_out9, twos_complementer_1_bit16_result[6]);
  and and_16 (and_16_out, demultiplexer_3_out8, twos_complementer_1_bit16_result[7]);
  or or_9 (or_9_out[0], and_7_out, and_8_out, and_9_out, and_11_out, and_12_out, and_13_out, and_15_out, and_16_out, and_17_out, and_18_out, and_19_out, and_20_out, and_21_out, and_22_out, and_23_out, and_24_out);
  // Probe on {or_10_out[14:0], or_9_out[0]}
  // Probe on {bit16_add_1_bit16_result, bit16_add_1_bit16_result_2}
  Twos_Complementer twos_complementer_3 (
    .Allow_Twos_Complement(or_2_out), .Bit16_Input(or_7_out), .Bit16_Result(twos_complementer_3_bit16_result));  // open: Floating_Point_Bit_Strip, Cut_MSB
  S_R_Flip_Flop s_r_ff_9 (
    .S(demultiplexer_2_out7), .R(in_2), .clk(and_6_out), .Q(s_r_ff_16_q[7]), .reset(not_3_out));  // open: Qn, preset
  and and_17 (and_17_out, demultiplexer_3_out7, twos_complementer_1_bit16_result[8]);
  and and_18 (and_18_out, demultiplexer_3_out6, twos_complementer_1_bit16_result[9]);
  and and_19 (and_19_out, demultiplexer_3_out5, twos_complementer_1_bit16_result[10]);
  assign or_10_out = bit16_controlled_buffer_5_bit16_out | bit16_controlled_buffer_6_bit16_out;  // OR_Gate or_10, 16 bits wide
  Bit16_Controlled_Buffer bit16_controlled_buffer_5 (
    .Enable(not_5_out), .Bit16_In(register_1_q), .Bit16_Out(bit16_controlled_buffer_5_bit16_out));
  Bit16_Controlled_Buffer bit16_controlled_buffer_6 (
    .Enable(bit16_add_1_carry_out), .Bit16_In({bit16_add_1_bit16_result, bit16_add_1_bit16_result_2}),
    .Bit16_Out(bit16_controlled_buffer_6_bit16_out));
  Bit16_Controlled_Buffer bit16_controlled_buffer_7 (.Bit16_In(bit16_multiplier_1_lower_word));  // open: Enable, Bit16_Out
  Bit16_Controlled_Buffer bit16_controlled_buffer_8 (.Bit16_In(bit16_multiplier_1_upper_word));  // open: Enable, Bit16_Out
  Twos_Complementer twos_complementer_4 (
    .Allow_Twos_Complement(or_2_out), .Bit16_Input({bit16_add_1_bit16_result, bit16_add_1_bit16_result_2}),
    .Bit16_Result(twos_complementer_4_bit16_result));  // open: Floating_Point_Bit_Strip, Cut_MSB
  S_R_Flip_Flop s_r_ff_10 (
    .S(demultiplexer_2_out6), .R(in_2), .clk(and_6_out), .Q(s_r_ff_16_q[6]), .reset(not_3_out));  // open: Qn, preset
  and and_20 (and_20_out, demultiplexer_3_out4, twos_complementer_1_bit16_result[11]);
  and and_21 (and_21_out, demultiplexer_3_out3, twos_complementer_1_bit16_result[12]);
  and and_22 (and_22_out, demultiplexer_3_out2, twos_complementer_1_bit16_result[13]);
  // Probe on twos_complementer_4_bit16_result
  S_R_Flip_Flop s_r_ff_11 (
    .S(demultiplexer_2_out5), .R(in_2), .clk(and_6_out), .Q(s_r_ff_16_q[5]), .reset(not_3_out));  // open: Qn, preset
  and and_23 (and_23_out, demultiplexer_3_out1, twos_complementer_1_bit16_result[14]);
  and and_24 (and_24_out, demultiplexer_3_out0, twos_complementer_1_bit16_result[15]);
  S_R_Flip_Flop s_r_ff_12 (
    .S(demultiplexer_2_out4), .R(in_2), .clk(and_6_out), .Q(s_r_ff_16_q[4]), .reset(not_3_out));  // open: Qn, preset
  S_R_Flip_Flop s_r_ff_13 (
    .S(demultiplexer_2_out3), .R(in_2), .clk(and_6_out), .Q(s_r_ff_16_q[3]), .reset(not_3_out));  // open: Qn, preset
  Bit16_Controlled_Buffer bit16_controlled_buffer_9 (.Bit16_In({bit16_add_1_bit16_result, bit16_add_1_bit16_result_2}));  // open: Enable, Bit16_Out
  S_R_Flip_Flop s_r_ff_14 (
    .S(demultiplexer_2_out2), .R(in_2), .clk(and_6_out), .Q(s_r_ff_16_q[2]), .reset(not_3_out));  // open: Qn, preset
  or or_11 (Overflow, undriven[0], undriven[1], undriven[2], undriven[3], undriven[4], undriven[5], undriven[6], undriven[7], undriven[8], undriven[9], undriven[10], undriven[11], undriven[12], undriven[13], undriven[14], undriven[15]);
  S_R_Flip_Flop s_r_ff_15 (
    .S(demultiplexer_2_out1), .R(in_2), .clk(and_6_out), .Q(s_r_ff_16_q[1]), .reset(not_3_out));  // open: Qn, preset
  // OR_Gate or_12 has open pins: out=Bit16_Result
  S_R_Flip_Flop s_r_ff_16 (
    .S(demultiplexer_2_out0), .R(in_2), .clk(and_6_out), .Q(s_r_ff_16_q[0]), .reset(not_3_out));  // open: Qn, preset
  nor nor_3 (Zero, Bit16_Result[0], Bit16_Result[1], Bit16_Result[2], Bit16_Result[3], Bit16_Result[4], Bit16_Result[5], Bit16_Result[6], Bit16_Result[7], Bit16_Result[8], Bit16_Result[9], Bit16_Result[10], Bit16_Result[11], Bit16_Result[12], Bit16_Result[13], Bit16_Result[14], Bit16_Result[15]);

  // Notes on the sheet:
  //   FP OP
  //   FP DIV
  //   this line may go low 1 clock before its meant to
  //   LSB IS FAR LEFT. SPLITTER NEEDS INVERSION
  //   unsigned subtraction carry
endmodule

module Twos_Complementer (
  input  Floating_Point_Bit_Strip,
  input  Cut_MSB,
  input  Allow_Twos_Complement,
  input  [15:0] Bit16_Input,
  output [15:0] Bit16_Result
);

  wire and_1_out, and_2_out, and_3_out, and_4_out, and_5_out, and_6_out, and_7_out, and_8_out, and_9_out,
       and_10_out, and_11_out, and_12_out, and_13_out, and_14_out, and_15_out, or_1_out, or_2_out, or_3_out,
       or_4_out, or_5_out, or_6_out, or_7_out, or_8_out, or_9_out, or_10_out, or_11_out, or_12_out,
       or_13_out, or_14_out, or_15_out, xor_10_out, xor_11_out, xor_12_out, xor_13_out, xor_14_out,
       xor_15_out;

  or or_1 (or_1_out, Floating_Point_Bit_Strip, Cut_MSB);
  and and_1 (and_1_out, Bit16_Input[0], Allow_Twos_Complement);
  and and_2 (and_2_out, Bit16_Result[1], Allow_Twos_Complement);
  or or_2 (or_2_out, and_1_out, and_2_out);
  and and_3 (and_3_out, Bit16_Result[2], Allow_Twos_Complement);
  or or_3 (or_3_out, and_1_out, and_2_out, and_3_out);
  and and_4 (and_4_out, Bit16_Result[3], Allow_Twos_Complement);
  or or_4 (or_4_out, and_1_out, and_2_out, and_3_out, and_4_out);
  and and_5 (and_5_out, Bit16_Result[4], Allow_Twos_Complement);
  or or_5 (or_5_out, and_1_out, and_2_out, and_3_out, and_4_out, and_5_out);
  and and_6 (and_6_out, Bit16_Result[5], Allow_Twos_Complement);
  or or_6 (or_6_out, and_1_out, and_2_out, and_3_out, and_4_out, and_5_out, and_6_out);
  and and_7 (and_7_out, Bit16_Result[6], Allow_Twos_Complement);
  or or_7 (or_7_out, and_1_out, and_2_out, and_3_out, and_4_out, and_5_out, and_6_out, and_7_out);
  and and_8 (and_8_out, Bit16_Result[7], Allow_Twos_Complement);
  or or_8 (or_8_out, and_1_out, and_2_out, and_3_out, and_4_out, and_5_out, and_6_out, and_7_out, and_8_out);
  and and_9 (and_9_out, Bit16_Result[8], Allow_Twos_Complement);
  or or_9 (or_9_out, and_1_out, and_2_out, and_3_out, and_4_out, and_5_out, and_6_out, and_7_out, and_8_out, and_9_out);
  and and_10 (and_10_out, Bit16_Result[9], Allow_Twos_Complement);
  or or_10 (or_10_out, and_1_out, and_2_out, and_3_out, and_4_out, and_5_out, and_6_out, and_7_out, and_8_out, and_9_out, and_10_out);
  and and_11 (and_11_out, xor_10_out, Allow_Twos_Complement);
  or or_11 (or_11_out, and_1_out, and_2_out, and_3_out, and_4_out, and_5_out, and_6_out, and_7_out, and_8_out, and_9_out, and_10_out, and_11_out);
  and and_12 (and_12_out, xor_11_out, Allow_Twos_Complement);
  or or_12 (or_12_out, and_1_out, and_2_out, and_3_out, and_4_out, and_5_out, and_6_out, and_7_out, and_8_out, and_9_out, and_10_out, and_11_out, and_12_out);
  and and_13 (and_13_out, xor_12_out, Allow_Twos_Complement);
  or or_13 (or_13_out, and_1_out, and_2_out, and_3_out, and_4_out, and_5_out, and_6_out, and_7_out, and_8_out, and_9_out, and_10_out, and_11_out, and_12_out, and_13_out);
  and and_14 (and_14_out, xor_13_out, Allow_Twos_Complement);
  or or_14 (or_14_out, and_1_out, and_2_out, and_3_out, and_4_out, and_5_out, and_6_out, and_7_out, and_8_out, and_9_out, and_10_out, and_11_out, and_12_out, and_13_out, and_14_out);
  and and_15 (and_15_out, xor_14_out, Allow_Twos_Complement);
  or or_15 (or_15_out, and_1_out, and_2_out, and_3_out, and_4_out, and_5_out, and_6_out, and_7_out, and_8_out, and_9_out, and_10_out, and_11_out, and_12_out, and_13_out, and_14_out, and_15_out);
  xor xor_1 (Bit16_Result[1], and_1_out, Bit16_Input[1]);
  xor xor_2 (Bit16_Result[2], or_2_out, Bit16_Input[2]);
  xor xor_3 (Bit16_Result[3], or_3_out, Bit16_Input[3]);
  xor xor_4 (Bit16_Result[4], or_4_out, Bit16_Input[4]);
  xor xor_5 (Bit16_Result[5], or_5_out, Bit16_Input[5]);
  xor xor_6 (Bit16_Result[6], or_6_out, Bit16_Input[6]);
  xor xor_7 (Bit16_Result[7], or_7_out, Bit16_Input[7]);
  xor xor_8 (Bit16_Result[8], or_8_out, Bit16_Input[8]);
  xor xor_9 (Bit16_Result[9], or_9_out, Bit16_Input[9]);
  xor xor_10 (xor_10_out, or_10_out, Bit16_Input[10]);
  xor xor_11 (xor_11_out, or_11_out, Bit16_Input[11]);
  xor xor_12 (xor_12_out, or_12_out, Bit16_Input[12]);
  xor xor_13 (xor_13_out, or_13_out, Bit16_Input[13]);
  xor xor_14 (xor_14_out, or_14_out, Bit16_Input[14]);
  and and_16 (Bit16_Result[15], ~or_1_out, xor_15_out);  // AND_Gate
  xor xor_15 (xor_15_out, or_15_out, Bit16_Input[15]);
  or or_16 (Bit16_Result[10], Floating_Point_Bit_Strip, xor_10_out);
  and and_17 (Bit16_Result[11], ~Floating_Point_Bit_Strip, xor_11_out);  // AND_Gate
  and and_18 (Bit16_Result[12], ~Floating_Point_Bit_Strip, xor_12_out);  // AND_Gate
  and and_19 (Bit16_Result[13], ~Floating_Point_Bit_Strip, xor_13_out);  // AND_Gate
  and and_20 (Bit16_Result[14], ~Floating_Point_Bit_Strip, xor_14_out);  // AND_Gate

  assign Bit16_Result[0] = Bit16_Input[0];

  // Notes on the sheet:
  //   bc "implied" leading bit
endmodule
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module Bit16_Divider (
  input  [15:0] Bit16_Dividend,
  input  [15:0] Bit16_Divisor,
  output [15:0] Bit16_Quotient,
  output [15:0] Bit16_Remainder
);

  wire and_1_out, and_2_out, and_3_out, and_4_out, and_5_out, and_6_out, and_7_out, and_8_out, and_9_out,
       and_10_out, and_11_out, and_12_out, and_13_out, and_14_out, and_15_out, not_1_out, not_2_out,
       not_3_out, not_4_out, not_5_out, not_6_out, not_7_out, not_8_out, not_9_out, not_10_out, not_11_out,
       not_12_out, not_13_out, not_14_out, not_15_out, not_16_out, or_1_out, or_2_out, or_3_out, or_4_out,
       or_5_out, or_6_out, or_7_out, or_8_out, or_9_out, or_10_out, or_11_out, or_12_out, or_13_out,
       or_14_out;
  wire [15:0] bit16_add_16_p3, bit16_controlled_buffer_1_bit16_out, bit16_controlled_buffer_2_bit16_out,
       bit16_controlled_buffer_3_bit16_out, bit16_controlled_buffer_4_bit16_out,
       bit16_controlled_buffer_5_bit16_out, bit16_controlled_buffer_6_bit16_out,
       bit16_controlled_buffer_7_bit16_out, bit16_controlled_buffer_8_bit16_out,
       bit16_controlled_buffer_9_bit16_out, bit16_controlled_buffer_10_bit16_out,
       bit16_controlled_buffer_11_bit16_out, bit16_controlled_buffer_12_bit16_out,
       bit16_controlled_buffer_13_bit16_out, bit16_controlled_buffer_14_bit16_out,
       bit16_controlled_buffer_15_bit16_out, bit16_controlled_buffer_16_bit16_out,
       bit16_controlled_buffer_17_bit16_out, bit16_controlled_buffer_18_bit16_out,
       bit16_controlled_buffer_19_bit16_out, bit16_controlled_buffer_20_bit16_out,
       bit16_controlled_buffer_21_bit16_out, bit16_controlled_buffer_22_bit16_out,
       bit16_controlled_buffer_23_bit16_out, bit16_controlled_buffer_24_bit16_out,
       bit16_controlled_buffer_25_bit16_out, bit16_controlled_buffer_26_bit16_out,
       bit16_controlled_buffer_27_bit16_out, bit16_controlled_buffer_28_bit16_out,
       bit16_controlled_buffer_29_bit16_out, bit16_controlled_buffer_30_bit16_out,
       bit16_controlled_buffer_31_bit16_out, bit16_controlled_buffer_32_bit16_out, or_29_out;
  wire [15:1] bit16_add_1_p3, bit16_add_2_p3, bit16_add_3_p3, bit16_add_4_p3, bit16_add_5_p3, bit16_add_6_p3,
       bit16_add_7_p3, bit16_add_8_p3, bit16_add_9_p3, bit16_add_10_p3, bit16_add_11_p3, bit16_add_12_p3,
       bit16_add_13_p3, bit16_add_14_p3, bit16_add_15_p3, or_15_out, or_16_out, or_17_out, or_18_out,
       or_19_out, or_20_out, or_21_out, or_22_out, or_23_out, or_24_out, or_25_out, or_26_out, or_27_out,
       or_28_out, xor_1_out;
  wire [15:15] bit16_add_1_p3_2, bit16_add_2_p3_2, bit16_add_3_p3_2, bit16_add_4_p3_2, bit16_add_5_p3_2,
       bit16_add_6_p3_2, bit16_add_7_p3_2, bit16_add_8_p3_2, bit16_add_9_p3_2, bit16_add_10_p3_2,
       bit16_add_11_p3_2, bit16_add_12_p3_2, bit16_add_13_p3_2, bit16_add_14_p3_2, bit16_add_15_p3_2,
       or_15_out_2, or_16_out_2, or_17_out_2, or_18_out_2, or_19_out_2, or_20_out_2, or_21_out_2,
       or_22_out_2, or_23_out_2, or_24_out_2, or_25_out_2, or_26_out_2, or_27_out_2, or_28_out_2;

  and and_1 (and_1_out, Bit16_Divisor[0], 1'b1);
  and and_2 (and_2_out, xor_1_out[1], 1'b1);
  or or_1 (or_1_out, and_1_out, and_2_out);
  and and_3 (and_3_out, xor_1_out[2], 1'b1);
  or or_2 (or_2_out, and_1_out, and_2_out, and_3_out);
  and and_4 (and_4_out, xor_1_out[3], 1'b1);
  or or_3 (or_3_out, and_1_out, and_2_out, and_3_out, and_4_out);
  and and_5 (and_5_out, xor_1_out[4], 1'b1);
  or or_4 (or_4_out, and_1_out, and_2_out, and_3_out, and_4_out, and_5_out);
  and and_6 (and_6_out, xor_1_out[5], 1'b1);
  or or_5 (or_5_out, and_1_out, and_2_out, and_3_out, and_4_out, and_5_out, and_6_out);
  and and_7 (and_7_out, xor_1_out[6], 1'b1);
  or or_6 (or_6_out, and_1_out, and_2_out, and_3_out, and_4_out, and_5_out, and_6_out, and_7_out);
  and and_8 (and_8_out, xor_1_out[7], 1'b1);
  or or_7 (or_7_out, and_1_out, and_2_out, and_3_out, and_4_out, and_5_out, and_6_out, and_7_out, and_8_out);
  and and_9 (and_9_out, xor_1_out[8], 1'b1);
  or or_8 (or_8_out, and_1_out, and_2_out, and_3_out, and_4_out, and_5_out, and_6_out, and_7_out, and_8_out, and_9_out);
  and and_10 (and_10_out, xor_1_out[9], 1'b1);
  or or_9 (or_9_out, and_1_out, and_2_out, and_3_out, and_4_out, and_5_out, and_6_out, and_7_out, and_8_out, and_9_out, and_10_out);
  and and_11 (and_11_out, xor_1_out[10], 1'b1);
  or or_10 (or_10_out, and_1_out, and_2_out, and_3_out, and_4_out, and_5_out, and_6_out, and_7_out, and_8_out, and_9_out, and_10_out, and_11_out);
  and and_12 (and_12_out, xor_1_out[11], 1'b1);
  or or_11 (or_11_out, and_1_out, and_2_out, and_3_out, and_4_out, and_5_out, and_6_out, and_7_out, and_8_out, and_9_out, and_10_out, and_11_out, and_12_out);
  and and_13 (and_13_out, xor_1_out[12], 1'b1);
  or or_12 (or_12_out, and_1_out, and_2_out, and_3_out, and_4_out, and_5_out, and_6_out, and_7_out, and_8_out, and_9_out, and_10_out, and_11_out, and_12_out, and_13_out);
  and and_14 (and_14_out, xor_1_out[13], 1'b1);
  or or_13 (or_13_out, and_1_out, and_2_out, and_3_out, and_4_out, and_5_out, and_6_out, and_7_out, and_8_out, and_9_out, and_10_out, and_11_out, and_12_out, and_13_out, and_14_out);
  and and_15 (and_15_out, xor_1_out[14], 1'b1);
  or or_14 (or_14_out, and_1_out, and_2_out, and_3_out, and_4_out, and_5_out, and_6_out, and_7_out, and_8_out, and_9_out, and_10_out, and_11_out, and_12_out, and_13_out, and_14_out, and_15_out);
  xor xor_1 (xor_1_out[1], and_1_out, Bit16_Divisor[1]);
  xor xor_2 (xor_1_out[2], or_1_out, Bit16_Divisor[2]);
  xor xor_3 (xor_1_out[3], or_2_out, Bit16_Divisor[3]);
  xor xor_4 (xor_1_out[4], or_3_out, Bit16_Divisor[4]);
  xor xor_5 (xor_1_out[5], or_4_out, Bit16_Divisor[5]);
  xor xor_6 (xor_1_out[6], or_5_out, Bit16_Divisor[6]);
  xor xor_7 (xor_1_out[7], or_6_out, Bit16_Divisor[7]);
  xor xor_8 (xor_1_out[8], or_7_out, Bit16_Divisor[8]);
  xor xor_9 (xor_1_out[9], or_8_out, Bit16_Divisor[9]);
  xor xor_10 (xor_1_out[10], or_9_out, Bit16_Divisor[10]);
  xor xor_11 (xor_1_out[11], or_10_out, Bit16_Divisor[11]);
  xor xor_12 (xor_1_out[12], or_11_out, Bit16_Divisor[12]);
  xor xor_13 (xor_1_out[13], or_12_out, Bit16_Divisor[13]);
  xor xor_14 (xor_1_out[14], or_13_out, Bit16_Divisor[14]);
  xor xor_15 (xor_1_out[15], or_14_out, Bit16_Divisor[15]);
  not not_1 (not_1_out, Bit16_Quotient[15]);
  not not_2 (not_2_out, Bit16_Quotient[14]);
  not not_3 (not_3_out, Bit16_Quotient[13]);
  not not_4 (not_4_out, Bit16_Quotient[12]);
  not not_5 (not_5_out, Bit16_Quotient[11]);
  not not_6 (not_6_out, Bit16_Quotient[10]);
  not not_7 (not_7_out, Bit16_Quotient[9]);
  not not_8 (not_8_out, Bit16_Quotient[8]);
  not not_9 (not_9_out, Bit16_Quotient[7]);
  not not_10 (not_10_out, Bit16_Quotient[6]);
  not not_11 (not_11_out, Bit16_Quotient[5]);
  not not_12 (not_12_out, Bit16_Quotient[4]);
  not not_13 (not_13_out, Bit16_Quotient[3]);
  not not_14 (not_14_out, Bit16_Quotient[2]);
  not not_15 (not_15_out, Bit16_Quotient[1]);
  not not_16 (not_16_out, Bit16_Quotient[0]);
  Bit16_Controlled_Buffer bit16_controlled_buffer_1 (
    .Enable(Bit16_Quotient[15]), .Bit16_In({bit16_add_11_p3, Bit16_Dividend[14]}),
    .Bit16_Out(bit16_controlled_buffer_1_bit16_out));
  Bit16_Controlled_Buffer bit16_controlled_buffer_2 (
    .Enable(not_1_out), .Bit16_In({{14{1'b0}}, Bit16_Dividend[15:14]}),
    .Bit16_Out(bit16_controlled_buffer_2_bit16_out));
  assign {or_15_out_2[15], or_15_out} = bit16_controlled_buffer_2_bit16_out | bit16_controlled_buffer_1_bit16_out;  // OR_Gate or_15, 16 bits wide
  // Bit16_Add bit16_add_1: pin names not known; wires that end beside it: {or_15_out_2[15], or_15_out}, {xor_1_out, Bit16_Divisor[0]}, {bit16_add_1_p3_2[15], bit16_add_1_p3}, Bit16_Quotient[14]
  Bit16_Controlled_Buffer bit16_controlled_buffer_3 (
    .Enable(Bit16_Quotient[14]), .Bit16_In({bit16_add_1_p3, Bit16_Dividend[13]}),
    .Bit16_Out(bit16_controlled_buffer_3_bit16_out));
  Bit16_Controlled_Buffer bit16_controlled_buffer_4 (
    .Enable(not_2_out), .Bit16_In({or_15_out, Bit16_Dividend[13]}),
    .Bit16_Out(bit16_controlled_buffer_4_bit16_out));
  assign {or_16_out_2[15], or_16_out} = bit16_controlled_buffer_4_bit16_out | bit16_controlled_buffer_3_bit16_out;  // OR_Gate or_16, 16 bits wide
  // Bit16_Add bit16_add_2: pin names not known; wires that end beside it: {xor_1_out, Bit16_Divisor[0]}, {or_16_out_2[15], or_16_out}, {bit16_add_2_p3_2[15], bit16_add_2_p3}, Bit16_Quotient[13]
  Bit16_Controlled_Buffer bit16_controlled_buffer_5 (
    .Enable(Bit16_Quotient[13]), .Bit16_In({bit16_add_2_p3, Bit16_Dividend[12]}),
    .Bit16_Out(bit16_controlled_buffer_5_bit16_out));
  Bit16_Controlled_Buffer bit16_controlled_buffer_6 (
    .Enable(not_3_out), .Bit16_In({or_16_out, Bit16_Dividend[12]}),
    .Bit16_Out(bit16_controlled_buffer_6_bit16_out));
  assign {or_17_out_2[15], or_17_out} = bit16_controlled_buffer_6_bit16_out | bit16_controlled_buffer_5_bit16_out;  // OR_Gate or_17, 16 bits wide
  // Bit16_Add bit16_add_3: pin names not known; wires that end beside it: {xor_1_out, Bit16_Divisor[0]}, {or_17_out_2[15], or_17_out}, {bit16_add_3_p3_2[15], bit16_add_3_p3}, Bit16_Quotient[12]
  Bit16_Controlled_Buffer bit16_controlled_buffer_7 (
    .Enable(Bit16_Quotient[12]), .Bit16_In({bit16_add_3_p3, Bit16_Dividend[11]}),
    .Bit16_Out(bit16_controlled_buffer_7_bit16_out));
  Bit16_Controlled_Buffer bit16_controlled_buffer_8 (
    .Enable(not_4_out), .Bit16_In({or_17_out, Bit16_Dividend[11]}),
    .Bit16_Out(bit16_controlled_buffer_8_bit16_out));
  assign {or_18_out_2[15], or_18_out} = bit16_controlled_buffer_8_bit16_out | bit16_controlled_buffer_7_bit16_out;  // OR_Gate or_18, 16 bits wide
  // Bit16_Add bit16_add_4: pin names not known; wires that end beside it: {or_18_out_2[15], or_18_out}, {xor_1_out, Bit16_Divisor[0]}, {bit16_add_4_p3_2[15], bit16_add_4_p3}, Bit16_Quotient[11]
  Bit16_Controlled_Buffer bit16_controlled_buffer_9 (
    .Enable(Bit16_Quotient[11]), .Bit16_In({bit16_add_4_p3, Bit16_Dividend[10]}),
    .Bit16_Out(bit16_controlled_buffer_9_bit16_out));
  Bit16_Controlled_Buffer bit16_controlled_buffer_10 (
    .Enable(not_5_out), .Bit16_In({or_18_out, Bit16_Dividend[10]}),
    .Bit16_Out(bit16_controlled_buffer_10_bit16_out));
  assign {or_19_out_2[15], or_19_out} = bit16_controlled_buffer_10_bit16_out | bit16_controlled_buffer_9_bit16_out;  // OR_Gate or_19, 16 bits wide
  Bit16_Controlled_Buffer bit16_controlled_buffer_11 (
    .Enable(Bit16_Quotient[10]), .Bit16_In({bit16_add_12_p3, Bit16_Dividend[9]}),
    .Bit16_Out(bit16_controlled_buffer_11_bit16_out));
  Bit16_Controlled_Buffer bit16_controlled_buffer_12 (
    .Enable(not_6_out), .Bit16_In({or_19_out, Bit16_Dividend[9]}),
    .Bit16_Out(bit16_controlled_buffer_12_bit16_out));
  assign {or_20_out_2[15], or_20_out} = bit16_controlled_buffer_12_bit16_out | bit16_controlled_buffer_11_bit16_out;  // OR_Gate or_20, 16 bits wide
  // Bit16_Add bit16_add_5: pin names not known; wires that end beside it: {or_20_out_2[15], or_20_out}, {xor_1_out, Bit16_Divisor[0]}, {bit16_add_5_p3_2[15], bit16_add_5_p3}, Bit16_Quotient[9]
  Bit16_Controlled_Buffer bit16_controlled_buffer_13 (
    .Enable(Bit16_Quotient[9]), .Bit16_In({bit16_add_5_p3, Bit16_Dividend[8]}),
    .Bit16_Out(bit16_controlled_buffer_13_bit16_out));
  Bit16_Controlled_Buffer bit16_controlled_buffer_14 (
    .Enable(not_7_out), .Bit16_In({or_20_out, Bit16_Dividend[8]}),
    .Bit16_Out(bit16_controlled_buffer_14_bit16_out));
  assign {or_21_out_2[15], or_21_out} = bit16_controlled_buffer_14_bit16_out | bit16_controlled_buffer_13_bit16_out;  // OR_Gate or_21, 16 bits wide
  Bit16_Controlled_Buffer bit16_controlled_buffer_15 (
    .Enable(Bit16_Quotient[8]), .Bit16_In({bit16_add_13_p3, Bit16_Dividend[7]}),
    .Bit16_Out(bit16_controlled_buffer_15_bit16_out));
  Bit16_Controlled_Buffer bit16_controlled_buffer_16 (
    .Enable(not_8_out), .Bit16_In({or_21_out, Bit16_Dividend[7]}),
    .Bit16_Out(bit16_controlled_buffer_16_bit16_out));
  assign {or_22_out_2[15], or_22_out} = bit16_controlled_buffer_16_bit16_out | bit16_controlled_buffer_15_bit16_out;  // OR_Gate or_22, 16 bits wide
  Bit16_Controlled_Buffer bit16_controlled_buffer_17 (
    .Enable(Bit16_Quotient[7]), .Bit16_In({bit16_add_14_p3, Bit16_Dividend[6]}),
    .Bit16_Out(bit16_controlled_buffer_17_bit16_out));
  Bit16_Controlled_Buffer bit16_controlled_buffer_18 (
    .Enable(not_9_out), .Bit16_In({or_22_out, Bit16_Dividend[6]}),
    .Bit16_Out(bit16_controlled_buffer_18_bit16_out));
  assign {or_23_out_2[15], or_23_out} = bit16_controlled_buffer_18_bit16_out | bit16_controlled_buffer_17_bit16_out;  // OR_Gate or_23, 16 bits wide
  // Bit16_Add bit16_add_6: pin names not known; wires that end beside it: {or_23_out_2[15], or_23_out}, {xor_1_out, Bit16_Divisor[0]}, {bit16_add_6_p3_2[15], bit16_add_6_p3}, Bit16_Quotient[6]
  Bit16_Controlled_Buffer bit16_controlled_buffer_19 (
    .Enable(Bit16_Quotient[6]), .Bit16_In({bit16_add_6_p3, Bit16_Dividend[5]}),
    .Bit16_Out(bit16_controlled_buffer_19_bit16_out));
  Bit16_Controlled_Buffer bit16_controlled_buffer_20 (
    .Enable(not_10_out), .Bit16_In({or_23_out, Bit16_Dividend[5]}),
    .Bit16_Out(bit16_controlled_buffer_20_bit16_out));
  assign {or_24_out_2[15], or_24_out} = bit16_controlled_buffer_20_bit16_out | bit16_controlled_buffer_19_bit16_out;  // OR_Gate or_24, 16 bits wide
  // Bit16_Add bit16_add_7: pin names not known; wires that end beside it: {or_24_out_2[15], or_24_out}, {xor_1_out, Bit16_Divisor[0]}, {bit16_add_7_p3_2[15], bit16_add_7_p3}, Bit16_Quotient[5]
  Bit16_Controlled_Buffer bit16_controlled_buffer_21 (
    .Enable(Bit16_Quotient[5]), .Bit16_In({bit16_add_7_p3, Bit16_Dividend[4]}),
    .Bit16_Out(bit16_controlled_buffer_21_bit16_out));
  Bit16_Controlled_Buffer bit16_controlled_buffer_22 (
    .Enable(not_11_out), .Bit16_In({or_24_out, Bit16_Dividend[4]}),
    .Bit16_Out(bit16_controlled_buffer_22_bit16_out));
  assign {or_25_out_2[15], or_25_out} = bit16_controlled_buffer_22_bit16_out | bit16_controlled_buffer_21_bit16_out;  // OR_Gate or_25, 16 bits wide
  // Bit16_Add bit16_add_8: pin names not known; wires that end beside it: {or_25_out_2[15], or_25_out}, {xor_1_out, Bit16_Divisor[0]}, {bit16_add_8_p3_2[15], bit16_add_8_p3}, Bit16_Quotient[4]
  Bit16_Controlled_Buffer bit16_controlled_buffer_23 (
    .Enable(Bit16_Quotient[4]), .Bit16_In({bit16_add_8_p3, Bit16_Dividend[3]}),
    .Bit16_Out(bit16_controlled_buffer_23_bit16_out));
  Bit16_Controlled_Buffer bit16_controlled_buffer_24 (
    .Enable(not_12_out), .Bit16_In({or_25_out, Bit16_Dividend[3]}),
    .Bit16_Out(bit16_controlled_buffer_24_bit16_out));
  assign {or_26_out_2[15], or_26_out} = bit16_controlled_buffer_24_bit16_out | bit16_controlled_buffer_23_bit16_out;  // OR_Gate or_26, 16 bits wide
  // Bit16_Add bit16_add_9: pin names not known; wires that end beside it: {or_26_out_2[15], or_26_out}, {xor_1_out, Bit16_Divisor[0]}, {bit16_add_9_p3_2[15], bit16_add_9_p3}, Bit16_Quotient[3]
  Bit16_Controlled_Buffer bit16_controlled_buffer_25 (
    .Enable(Bit16_Quotient[3]), .Bit16_In({bit16_add_9_p3, Bit16_Dividend[2]}),
    .Bit16_Out(bit16_controlled_buffer_25_bit16_out));
  Bit16_Controlled_Buffer bit16_controlled_buffer_26 (
    .Enable(not_13_out), .Bit16_In({or_26_out, Bit16_Dividend[2]}),
    .Bit16_Out(bit16_controlled_buffer_26_bit16_out));
  assign {or_27_out_2[15], or_27_out} = bit16_controlled_buffer_26_bit16_out | bit16_controlled_buffer_25_bit16_out;  // OR_Gate or_27, 16 bits wide
  // Bit16_Add bit16_add_10: pin names not known; wires that end beside it: {or_27_out_2[15], or_27_out}, {xor_1_out, Bit16_Divisor[0]}, {bit16_add_10_p3_2[15], bit16_add_10_p3}, Bit16_Quotient[2]
  Bit16_Controlled_Buffer bit16_controlled_buffer_27 (
    .Enable(Bit16_Quotient[2]), .Bit16_In({bit16_add_10_p3, Bit16_Dividend[1]}),
    .Bit16_Out(bit16_controlled_buffer_27_bit16_out));
  Bit16_Controlled_Buffer bit16_controlled_buffer_28 (
    .Enable(not_14_out), .Bit16_In({or_27_out, Bit16_Dividend[1]}),
    .Bit16_Out(bit16_controlled_buffer_28_bit16_out));
  assign {or_28_out_2[15], or_28_out} = bit16_controlled_buffer_28_bit16_out | bit16_controlled_buffer_27_bit16_out;  // OR_Gate or_28, 16 bits wide
  Bit16_Controlled_Buffer bit16_controlled_buffer_29 (
    .Enable(Bit16_Quotient[1]), .Bit16_In({bit16_add_15_p3, Bit16_Dividend[0]}),
    .Bit16_Out(bit16_controlled_buffer_29_bit16_out));
  Bit16_Controlled_Buffer bit16_controlled_buffer_30 (
    .Enable(not_15_out), .Bit16_In({or_28_out, Bit16_Dividend[0]}),
    .Bit16_Out(bit16_controlled_buffer_30_bit16_out));
  assign or_29_out = bit16_controlled_buffer_30_bit16_out | bit16_controlled_buffer_29_bit16_out;  // OR_Gate or_29, 16 bits wide
  Bit16_Controlled_Buffer bit16_controlled_buffer_31 (
    .Enable(Bit16_Quotient[0]), .Bit16_In(bit16_add_16_p3), .Bit16_Out(bit16_controlled_buffer_31_bit16_out));
  Bit16_Controlled_Buffer bit16_controlled_buffer_32 (
    .Enable(not_16_out), .Bit16_In(or_29_out), .Bit16_Out(bit16_controlled_buffer_32_bit16_out));
  // Bit16_Add bit16_add_11: pin names not known; wires that end beside it: {xor_1_out, Bit16_Divisor[0]}, {{15{1'b0}}, Bit16_Dividend[15]}, {bit16_add_11_p3_2[15], bit16_add_11_p3}, Bit16_Quotient[15]
  // Bit16_Add bit16_add_12: pin names not known; wires that end beside it: {xor_1_out, Bit16_Divisor[0]}, {or_19_out_2[15], or_19_out}, {bit16_add_12_p3_2[15], bit16_add_12_p3}, Bit16_Quotient[10]
  // Bit16_Add bit16_add_13: pin names not known; wires that end beside it: {xor_1_out, Bit16_Divisor[0]}, {or_21_out_2[15], or_21_out}, {bit16_add_13_p3_2[15], bit16_add_13_p3}, Bit16_Quotient[8]
  // Bit16_Add bit16_add_14: pin names not known; wires that end beside it: {or_22_out_2[15], or_22_out}, {xor_1_out, Bit16_Divisor[0]}, {bit16_add_14_p3_2[15], bit16_add_14_p3}, Bit16_Quotient[7]
  // Bit16_Add bit16_add_15: pin names not known; wires that end beside it: {or_28_out_2[15], or_28_out}, {xor_1_out, Bit16_Divisor[0]}, {bit16_add_15_p3_2[15], bit16_add_15_p3}, Bit16_Quotient[1]
  // Bit16_Add bit16_add_16: pin names not known; wires that end beside it: {xor_1_out, Bit16_Divisor[0]}, or_29_out, bit16_add_16_p3, Bit16_Quotient[0]
  assign Bit16_Remainder = bit16_controlled_buffer_32_bit16_out | bit16_controlled_buffer_31_bit16_out;  // OR_Gate or_30, 16 bits wide
  // Probe on Bit16_Quotient
  // Probe on Bit16_Remainder
endmodule

module Bit4_CLA_Logic (
  input  Cin,
  input  P1,
  input  G1,
  input  P2,
  input  G2,
  input  P3,
  input  G3,
  input  P4,
  input  G4,
  output C2,
  output C3,
  output C4,
  output COUT,
  output PG
);

  wire and_1_out, and_2_out, and_3_out, and_4_out, and_5_out, and_6_out, and_7_out, and_8_out, and_9_out,
       and_10_out;

  or or_1 (C2, G1, and_1_out);
  or or_2 (C3, G2, and_2_out, and_3_out);
  or or_3 (C4, G3, and_4_out, and_5_out, and_6_out);
  or or_4 (COUT, G4, and_7_out, and_8_out, and_9_out, and_10_out);
  and and_1 (and_1_out, P1, Cin);
  and and_2 (and_2_out, P2, G1);
  and and_3 (and_3_out, P2, P1, Cin);
  and and_4 (and_4_out, G2, P3);
  and and_5 (and_5_out, P3, P2, G1);
  and and_6 (and_6_out, P3, P2, Cin, P1);
  and and_7 (and_7_out, G3, P4);
  and and_8 (and_8_out, P4, P3, G2);
  and and_9 (and_9_out, P4, P3, P2, G1);
  and and_10 (and_10_out, P4, P3, P2, P1, Cin);
  and and_11 (PG, P1, P2, P3, P4);
endmodule

module Bit16_Left_Shift (
  input  [15:0] Bit16_Data,
  input  [3:0] Bit4_Shift,
  output [15:0] Bit16_Result,
  output Shift_Overflow
);

  wire and_1_out, and_2_out, and_3_out, and_4_out, and_5_out, and_6_out, and_7_out, and_8_out, and_9_out,
       and_10_out, and_11_out, and_12_out, and_13_out, and_14_out, and_15_out, and_16_out, and_17_out,
       and_18_out, and_19_out, and_20_out, and_21_out, and_22_out, and_23_out, and_24_out, and_25_out,
       and_26_out, and_27_out, and_28_out, and_29_out, and_30_out, and_31_out, and_32_out, and_33_out,
       and_34_out, and_35_out, and_36_out, and_37_out, and_38_out, and_39_out, and_40_out, and_41_out,
       and_42_out, and_43_out, and_44_out, and_45_out, and_46_out, and_47_out, and_48_out, and_49_out,
       and_50_out, and_51_out, and_52_out, and_53_out, and_54_out, and_55_out, and_56_out, and_57_out,
       and_58_out, and_59_out, and_60_out, and_61_out, and_62_out, and_63_out, and_64_out, and_65_out,
       and_66_out, and_67_out, and_69_out, and_70_out, and_71_out, and_72_out, and_73_out, and_74_out,
       and_75_out, and_77_out, and_78_out, and_79_out, and_80_out, and_81_out, and_82_out, and_83_out,
       and_85_out, and_86_out, and_87_out, and_88_out, and_89_out, and_90_out, and_91_out, and_93_out,
       and_94_out, and_95_out, and_96_out, and_97_out, and_98_out, and_99_out, and_101_out, and_102_out,
       and_103_out, and_104_out, and_105_out, and_106_out, and_107_out, and_109_out, and_110_out,
       and_111_out, and_112_out, and_113_out, and_114_out, and_115_out, and_117_out, and_118_out,
       and_119_out, and_120_out, and_121_out, and_122_out, and_123_out, and_125_out, and_126_out,
       and_127_out, and_128_out, or_2_out, or_3_out, or_4_out, or_6_out, or_7_out, or_8_out, or_10_out,
       or_11_out, or_12_out, or_14_out, or_15_out, or_16_out, or_18_out, or_19_out, or_20_out, or_22_out,
       or_23_out, or_24_out, or_26_out, or_27_out, or_28_out, or_30_out, or_31_out, or_32_out, or_34_out,
       or_35_out, or_36_out, or_37_out, or_38_out, or_39_out, or_40_out, or_41_out, or_42_out, or_43_out,
       or_44_out, or_45_out, or_46_out, or_47_out, or_48_out, or_49_out, or_50_out;

  or or_1 (Shift_Overflow, and_5_out, and_7_out, and_15_out, and_9_out, and_17_out, and_25_out, and_34_out, and_11_out, and_19_out, and_27_out, and_36_out, and_43_out, and_51_out, and_59_out, and_67_out);
  and and_1 (and_1_out, ~Bit4_Shift[0], Bit16_Data[15]);  // AND_Gate
  or or_2 (or_2_out, and_1_out, and_13_out);
  and and_2 (and_2_out, ~Bit4_Shift[1], or_2_out);  // AND_Gate
  or or_3 (or_3_out, and_2_out, and_23_out);
  and and_3 (and_3_out, ~Bit4_Shift[2], or_3_out);  // AND_Gate
  or or_4 (or_4_out, and_3_out, and_41_out);
  and and_4 (and_4_out, ~Bit4_Shift[3], or_4_out);  // AND_Gate
  or or_5 (Bit16_Result[15], and_4_out, and_75_out);
  and and_5 (and_5_out, Bit16_Data[15], Bit4_Shift[0]);
  and and_6 (and_6_out, ~Bit4_Shift[0], Bit16_Data[14]);  // AND_Gate
  or or_6 (or_6_out, and_6_out, and_21_out);
  and and_7 (and_7_out, or_2_out, Bit4_Shift[1]);
  and and_8 (and_8_out, ~Bit4_Shift[1], or_6_out);  // AND_Gate
  or or_7 (or_7_out, and_8_out, and_32_out);
  and and_9 (and_9_out, or_3_out, Bit4_Shift[2]);
  and and_10 (and_10_out, ~Bit4_Shift[2], or_7_out);  // AND_Gate
  or or_8 (or_8_out, and_10_out, and_49_out);
  and and_11 (and_11_out, or_4_out, Bit4_Shift[3]);
  and and_12 (and_12_out, ~Bit4_Shift[3], or_8_out);  // AND_Gate
  or or_9 (Bit16_Result[14], and_12_out, and_83_out);
  and and_13 (and_13_out, Bit16_Data[14], Bit4_Shift[0]);
  and and_14 (and_14_out, ~Bit4_Shift[0], Bit16_Data[13]);  // AND_Gate
  or or_10 (or_10_out, and_14_out, and_30_out);
  and and_15 (and_15_out, or_6_out, Bit4_Shift[1]);
  and and_16 (and_16_out, ~Bit4_Shift[1], or_10_out);  // AND_Gate
  or or_11 (or_11_out, and_16_out, and_39_out);
  and and_17 (and_17_out, or_7_out, Bit4_Shift[2]);
  and and_18 (and_18_out, ~Bit4_Shift[2], or_11_out);  // AND_Gate
  or or_12 (or_12_out, and_18_out, and_57_out);
  and and_19 (and_19_out, or_8_out, Bit4_Shift[3]);
  and and_20 (and_20_out, ~Bit4_Shift[3], or_12_out);  // AND_Gate
  or or_13 (Bit16_Result[13], and_20_out, and_91_out);
  and and_21 (and_21_out, Bit16_Data[13], Bit4_Shift[0]);
  and and_22 (and_22_out, ~Bit4_Shift[0], Bit16_Data[12]);  // AND_Gate
  or or_14 (or_14_out, and_22_out, and_37_out);
  and and_23 (and_23_out, or_10_out, Bit4_Shift[1]);
  and and_24 (and_24_out, ~Bit4_Shift[1], or_14_out);  // AND_Gate
  or or_15 (or_15_out, and_24_out, and_47_out);
  and and_25 (and_25_out, or_11_out, Bit4_Shift[2]);
  and and_26 (and_26_out, ~Bit4_Shift[2], or_15_out);  // AND_Gate
  or or_16 (or_16_out, and_26_out, and_65_out);
  and and_27 (and_27_out, or_12_out, Bit4_Shift[3]);
  and and_28 (and_28_out, ~Bit4_Shift[3], or_16_out);  // AND_Gate
  or or_17 (Bit16_Result[12], and_28_out, and_99_out);
  and and_29 (and_29_out, ~Bit4_Shift[0], Bit16_Data[11]);  // AND_Gate
  and and_30 (and_30_out, Bit16_Data[12], Bit4_Shift[0]);
  or or_18 (or_18_out, and_29_out, and_45_out);
  and and_31 (and_31_out, ~Bit4_Shift[1], or_18_out);  // AND_Gate
  and and_32 (and_32_out, or_14_out, Bit4_Shift[1]);
  or or_19 (or_19_out, and_31_out, and_55_out);
  and and_33 (and_33_out, ~Bit4_Shift[2], or_19_out);  // AND_Gate
  and and_34 (and_34_out, or_15_out, Bit4_Shift[2]);
  or or_20 (or_20_out, and_33_out, and_73_out);
  and and_35 (and_35_out, ~Bit4_Shift[3], or_20_out);  // AND_Gate
  and and_36 (and_36_out, or_16_out, Bit4_Shift[3]);
  or or_21 (Bit16_Result[11], and_35_out, and_107_out);
  and and_37 (and_37_out, Bit16_Data[11], Bit4_Shift[0]);
  and and_38 (and_38_out, ~Bit4_Shift[0], Bit16_Data[10]);  // AND_Gate
  or or_22 (or_22_out, and_38_out, and_53_out);
  and and_39 (and_39_out, or_18_out, Bit4_Shift[1]);
  and and_40 (and_40_out, ~Bit4_Shift[1], or_22_out);  // AND_Gate
  or or_23 (or_23_out, and_40_out, and_63_out);
  and and_41 (and_41_out, or_19_out, Bit4_Shift[2]);
  and and_42 (and_42_out, ~Bit4_Shift[2], or_23_out);  // AND_Gate
  or or_24 (or_24_out, and_42_out, and_81_out);
  and and_43 (and_43_out, or_20_out, Bit4_Shift[3]);
  and and_44 (and_44_out, ~Bit4_Shift[3], or_24_out);  // AND_Gate
  or or_25 (Bit16_Result[10], and_44_out, and_115_out);
  and and_45 (and_45_out, Bit16_Data[10], Bit4_Shift[0]);
  and and_46 (and_46_out, ~Bit4_Shift[0], Bit16_Data[9]);  // AND_Gate
  or or_26 (or_26_out, and_46_out, and_61_out);
  and and_47 (and_47_out, or_22_out, Bit4_Shift[1]);
  and and_48 (and_48_out, ~Bit4_Shift[1], or_26_out);  // AND_Gate
  or or_27 (or_27_out, and_48_out, and_71_out);
  and and_49 (and_49_out, or_23_out, Bit4_Shift[2]);
  and and_50 (and_50_out, ~Bit4_Shift[2], or_27_out);  // AND_Gate
  or or_28 (or_28_out, and_50_out, and_89_out);
  and and_51 (and_51_out, or_24_out, Bit4_Shift[3]);
  and and_52 (and_52_out, ~Bit4_Shift[3], or_28_out);  // AND_Gate
  or or_29 (Bit16_Result[9], and_52_out, and_123_out);
  and and_53 (and_53_out, Bit16_Data[9], Bit4_Shift[0]);
  and and_54 (and_54_out, ~Bit4_Shift[0], Bit16_Data[8]);  // AND_Gate
  or or_30 (or_30_out, and_54_out, and_69_out);
  and and_55 (and_55_out, or_26_out, Bit4_Shift[1]);
  and and_56 (and_56_out, ~Bit4_Shift[1], or_30_out);  // AND_Gate
  or or_31 (or_31_out, and_56_out, and_79_out);
  and and_57 (and_57_out, or_27_out, Bit4_Shift[2]);
  and and_58 (and_58_out, ~Bit4_Shift[2], or_31_out);  // AND_Gate
  or or_32 (or_32_out, and_58_out, and_97_out);
  and and_59 (and_59_out, or_28_out, Bit4_Shift[3]);
  and and_60 (and_60_out, ~Bit4_Shift[3], or_32_out);  // AND_Gate
  or or_33 (Bit16_Result[8], and_60_out, and_128_out);
  and and_61 (and_61_out, Bit16_Data[8], Bit4_Shift[0]);
  and and_62 (and_62_out, ~Bit4_Shift[0], Bit16_Data[7]);  // AND_Gate
  or or_34 (or_34_out, and_62_out, and_77_out);
  and and_63 (and_63_out, or_30_out, Bit4_Shift[1]);
  and and_64 (and_64_out, ~Bit4_Shift[1], or_34_out);  // AND_Gate
  or or_35 (or_35_out, and_64_out, and_87_out);
  and and_65 (and_65_out, or_31_out, Bit4_Shift[2]);
  and and_66 (and_66_out, ~Bit4_Shift[2], or_35_out);  // AND_Gate
  or or_36 (or_36_out, and_66_out, and_105_out);
  and and_67 (and_67_out, or_32_out, Bit4_Shift[3]);
  and and_68 (Bit16_Result[7], ~Bit4_Shift[3], or_36_out);  // AND_Gate
  and and_69 (and_69_out, Bit16_Data[7], Bit4_Shift[0]);
  and and_70 (and_70_out, ~Bit4_Shift[0], Bit16_Data[6]);  // AND_Gate
  or or_37 (or_37_out, and_70_out, and_85_out);
  and and_71 (and_71_out, or_34_out, Bit4_Shift[1]);
  and and_72 (and_72_out, ~Bit4_Shift[1], or_37_out);  // AND_Gate
  or or_38 (or_38_out, and_72_out, and_95_out);
  and and_73 (and_73_out, or_35_out, Bit4_Shift[2]);
  and and_74 (and_74_out, ~Bit4_Shift[2], or_38_out);  // AND_Gate
  or or_39 (or_39_out, and_74_out, and_113_out);
  and and_75 (and_75_out, or_36_out, Bit4_Shift[3]);
  and and_76 (Bit16_Result[6], ~Bit4_Shift[3], or_39_out);  // AND_Gate
  and and_77 (and_77_out, Bit16_Data[6], Bit4_Shift[0]);
  and and_78 (and_78_out, ~Bit4_Shift[0], Bit16_Data[5]);  // AND_Gate
  or or_40 (or_40_out, and_78_out, and_93_out);
  and and_79 (and_79_out, or_37_out, Bit4_Shift[1]);
  and and_80 (and_80_out, ~Bit4_Shift[1], or_40_out);  // AND_Gate
  or or_41 (or_41_out, and_80_out, and_103_out);
  and and_81 (and_81_out, or_38_out, Bit4_Shift[2]);
  and and_82 (and_82_out, ~Bit4_Shift[2], or_41_out);  // AND_Gate
  or or_42 (or_42_out, and_82_out, and_121_out);
  and and_83 (and_83_out, or_39_out, Bit4_Shift[3]);
  and and_84 (Bit16_Result[5], ~Bit4_Shift[3], or_42_out);  // AND_Gate
  and and_85 (and_85_out, Bit16_Data[5], Bit4_Shift[0]);
  and and_86 (and_86_out, ~Bit4_Shift[0], Bit16_Data[4]);  // AND_Gate
  or or_43 (or_43_out, and_86_out, and_101_out);
  and and_87 (and_87_out, or_40_out, Bit4_Shift[1]);
  and and_88 (and_88_out, ~Bit4_Shift[1], or_43_out);  // AND_Gate
  or or_44 (or_44_out, and_88_out, and_111_out);
  and and_89 (and_89_out, or_41_out, Bit4_Shift[2]);
  and and_90 (and_90_out, ~Bit4_Shift[2], or_44_out);  // AND_Gate
  or or_45 (or_45_out, and_90_out, and_127_out);
  and and_91 (and_91_out, or_42_out, Bit4_Shift[3]);
  and and_92 (Bit16_Result[4], ~Bit4_Shift[3], or_45_out);  // AND_Gate
  and and_93 (and_93_out, Bit16_Data[4], Bit4_Shift[0]);
  and and_94 (and_94_out, ~Bit4_Shift[0], Bit16_Data[3]);  // AND_Gate
  or or_46 (or_46_out, and_94_out, and_109_out);
  and and_95 (and_95_out, or_43_out, Bit4_Shift[1]);
  and and_96 (and_96_out, ~Bit4_Shift[1], or_46_out);  // AND_Gate
  or or_47 (or_47_out, and_96_out, and_119_out);
  and and_97 (and_97_out, or_44_out, Bit4_Shift[2]);
  and and_98 (and_98_out, ~Bit4_Shift[2], or_47_out);  // AND_Gate
  and and_99 (and_99_out, or_45_out, Bit4_Shift[3]);
  and and_100 (Bit16_Result[3], ~Bit4_Shift[3], and_98_out);  // AND_Gate
  and and_101 (and_101_out, Bit16_Data[3], Bit4_Shift[0]);
  and and_102 (and_102_out, ~Bit4_Shift[0], Bit16_Data[2]);  // AND_Gate
  or or_48 (or_48_out, and_102_out, and_117_out);
  and and_103 (and_103_out, or_46_out, Bit4_Shift[1]);
  and and_104 (and_104_out, ~Bit4_Shift[1], or_48_out);  // AND_Gate
  or or_49 (or_49_out, and_104_out, and_126_out);
  and and_105 (and_105_out, or_47_out, Bit4_Shift[2]);
  and and_106 (and_106_out, ~Bit4_Shift[2], or_49_out);  // AND_Gate
  and and_107 (and_107_out, and_98_out, Bit4_Shift[3]);
  and and_108 (Bit16_Result[2], ~Bit4_Shift[3], and_106_out);  // AND_Gate
  and and_109 (and_109_out, Bit16_Data[2], Bit4_Shift[0]);
  and and_110 (and_110_out, ~Bit4_Shift[0], Bit16_Data[1]);  // AND_Gate
  or or_50 (or_50_out, and_110_out, and_125_out);
  and and_111 (and_111_out, or_48_out, Bit4_Shift[1]);
  and and_112 (and_112_out, ~Bit4_Shift[1], or_50_out);  // AND_Gate
  and and_113 (and_113_out, or_49_out, Bit4_Shift[2]);
  and and_114 (and_114_out, ~Bit4_Shift[2], and_112_out);  // AND_Gate
  and and_115 (and_115_out, and_106_out, Bit4_Shift[3]);
  and and_116 (Bit16_Result[1], ~Bit4_Shift[3], and_114_out);  // AND_Gate
  and and_117 (and_117_out, Bit16_Data[1], Bit4_Shift[0]);
  and and_118 (and_118_out, ~Bit4_Shift[0], Bit16_Data[0]);  // AND_Gate
  and and_119 (and_119_out, or_50_out, Bit4_Shift[1]);
  and and_120 (and_120_out, ~Bit4_Shift[1], and_118_out);  // AND_Gate
  and and_121 (and_121_out, and_112_out, Bit4_Shift[2]);
  and and_122 (and_122_out, ~Bit4_Shift[2], and_120_out);  // AND_Gate
  and and_123 (and_123_out, and_114_out, Bit4_Shift[3]);
  and and_124 (Bit16_Result[0], ~Bit4_Shift[3], and_122_out);  // AND_Gate
  and and_125 (and_125_out, Bit16_Data[0], Bit4_Shift[0]);
  and and_126 (and_126_out, and_118_out, Bit4_Shift[1]);
  and and_127 (and_127_out, and_120_out, Bit4_Shift[2]);
  and and_128 (and_128_out, and_122_out, Bit4_Shift[3]);
endmodule

module Bit16_Right_Shift (
  input  [15:0] Bit16_Data,
  input  [3:0] Bit4_Shift,
  output [15:0] Bit16_Result,
  output Shift_Overflow
);

  wire and_1_out, and_2_out, and_3_out, and_4_out, and_5_out, and_6_out, and_7_out, and_8_out, and_9_out,
       and_10_out, and_11_out, and_12_out, and_13_out, and_14_out, and_15_out, and_16_out, and_17_out,
       and_18_out, and_19_out, and_20_out, and_21_out, and_22_out, and_23_out, and_24_out, and_25_out,
       and_26_out, and_27_out, and_28_out, and_29_out, and_30_out, and_31_out, and_32_out, and_33_out,
       and_34_out, and_35_out, and_36_out, and_37_out, and_38_out, and_39_out, and_40_out, and_41_out,
       and_42_out, and_43_out, and_44_out, and_45_out, and_46_out, and_47_out, and_48_out, and_49_out,
       and_50_out, and_51_out, and_52_out, and_53_out, and_54_out, and_55_out, and_56_out, and_57_out,
       and_58_out, and_59_out, and_60_out, and_61_out, and_62_out, and_63_out, and_64_out, and_65_out,
       and_66_out, and_67_out, and_69_out, and_70_out, and_71_out, and_72_out, and_73_out, and_74_out,
       and_75_out, and_77_out, and_78_out, and_79_out, and_80_out, and_81_out, and_82_out, and_83_out,
       and_85_out, and_86_out, and_87_out, and_88_out, and_89_out, and_90_out, and_91_out, and_93_out,
       and_94_out, and_95_out, and_96_out, and_97_out, and_98_out, and_99_out, and_101_out, and_102_out,
       and_103_out, and_104_out, and_105_out, and_106_out, and_107_out, and_109_out, and_110_out,
       and_111_out, and_112_out, and_113_out, and_114_out, and_115_out, and_117_out, and_118_out,
       and_119_out, and_120_out, and_121_out, and_122_out, and_123_out, and_125_out, and_126_out,
       and_127_out, and_128_out, or_2_out, or_3_out, or_4_out, or_6_out, or_7_out, or_8_out, or_10_out,
       or_11_out, or_12_out, or_14_out, or_15_out, or_16_out, or_18_out, or_19_out, or_20_out, or_22_out,
       or_23_out, or_24_out, or_26_out, or_27_out, or_28_out, or_30_out, or_31_out, or_32_out, or_34_out,
       or_35_out, or_36_out, or_37_out, or_38_out, or_39_out, or_40_out, or_41_out, or_42_out, or_43_out,
       or_44_out, or_45_out, or_46_out, or_47_out, or_48_out, or_49_out, or_50_out;

  or or_1 (Shift_Overflow, and_5_out, and_7_out, and_15_out, and_9_out, and_17_out, and_25_out, and_33_out, and_11_out, and_19_out, and_27_out, and_35_out, and_43_out, and_52_out, and_59_out, and_67_out);
  and and_1 (and_1_out, ~Bit4_Shift[0], Bit16_Data[0]);  // AND_Gate
  and and_2 (and_2_out, ~Bit4_Shift[1], or_2_out);  // AND_Gate
  and and_3 (and_3_out, ~Bit4_Shift[2], or_3_out);  // AND_Gate
  and and_4 (and_4_out, ~Bit4_Shift[3], or_4_out);  // AND_Gate
  and and_5 (and_5_out, Bit16_Data[0], Bit4_Shift[0]);
  and and_6 (and_6_out, ~Bit4_Shift[0], Bit16_Data[1]);  // AND_Gate
  or or_2 (or_2_out, and_1_out, and_13_out);
  and and_7 (and_7_out, or_2_out, Bit4_Shift[1]);
  and and_8 (and_8_out, ~Bit4_Shift[1], or_6_out);  // AND_Gate
  or or_3 (or_3_out, and_2_out, and_23_out);
  and and_9 (and_9_out, or_3_out, Bit4_Shift[2]);
  and and_10 (and_10_out, ~Bit4_Shift[2], or_7_out);  // AND_Gate
  or or_4 (or_4_out, and_3_out, and_41_out);
  and and_11 (and_11_out, or_4_out, Bit4_Shift[3]);
  and and_12 (and_12_out, ~Bit4_Shift[3], or_8_out);  // AND_Gate
  or or_5 (Bit16_Result[0], and_4_out, and_75_out);
  and and_13 (and_13_out, Bit16_Data[1], Bit4_Shift[0]);
  and and_14 (and_14_out, ~Bit4_Shift[0], Bit16_Data[2]);  // AND_Gate
  or or_6 (or_6_out, and_6_out, and_21_out);
  and and_15 (and_15_out, or_6_out, Bit4_Shift[1]);
  and and_16 (and_16_out, ~Bit4_Shift[1], or_10_out);  // AND_Gate
  or or_7 (or_7_out, and_8_out, and_31_out);
  and and_17 (and_17_out, or_7_out, Bit4_Shift[2]);
  and and_18 (and_18_out, ~Bit4_Shift[2], or_11_out);  // AND_Gate
  or or_8 (or_8_out, and_10_out, and_50_out);
  and and_19 (and_19_out, or_8_out, Bit4_Shift[3]);
  and and_20 (and_20_out, ~Bit4_Shift[3], or_12_out);  // AND_Gate
  or or_9 (Bit16_Result[1], and_12_out, and_83_out);
  and and_21 (and_21_out, Bit16_Data[2], Bit4_Shift[0]);
  and and_22 (and_22_out, ~Bit4_Shift[0], Bit16_Data[3]);  // AND_Gate
  or or_10 (or_10_out, and_14_out, and_29_out);
  and and_23 (and_23_out, or_10_out, Bit4_Shift[1]);
  and and_24 (and_24_out, ~Bit4_Shift[1], or_14_out);  // AND_Gate
  or or_11 (or_11_out, and_16_out, and_39_out);
  and and_25 (and_25_out, or_11_out, Bit4_Shift[2]);
  and and_26 (and_26_out, ~Bit4_Shift[2], or_15_out);  // AND_Gate
  or or_12 (or_12_out, and_18_out, and_57_out);
  and and_27 (and_27_out, or_12_out, Bit4_Shift[3]);
  and and_28 (and_28_out, ~Bit4_Shift[3], or_16_out);  // AND_Gate
  or or_13 (Bit16_Result[2], and_20_out, and_91_out);
  and and_29 (and_29_out, Bit16_Data[3], Bit4_Shift[0]);
  and and_30 (and_30_out, ~Bit4_Shift[0], Bit16_Data[4]);  // AND_Gate
  or or_14 (or_14_out, and_22_out, and_37_out);
  and and_31 (and_31_out, or_14_out, Bit4_Shift[1]);
  and and_32 (and_32_out, ~Bit4_Shift[1], or_18_out);  // AND_Gate
  or or_15 (or_15_out, and_24_out, and_48_out);
  and and_33 (and_33_out, or_15_out, Bit4_Shift[2]);
  and and_34 (and_34_out, ~Bit4_Shift[2], or_19_out);  // AND_Gate
  or or_16 (or_16_out, and_26_out, and_65_out);
  and and_35 (and_35_out, or_16_out, Bit4_Shift[3]);
  and and_36 (and_36_out, ~Bit4_Shift[3], or_20_out);  // AND_Gate
  or or_17 (Bit16_Result[3], and_28_out, and_99_out);
  and and_37 (and_37_out, Bit16_Data[4], Bit4_Shift[0]);
  and and_38 (and_38_out, ~Bit4_Shift[0], Bit16_Data[5]);  // AND_Gate
  or or_18 (or_18_out, and_30_out, and_46_out);
  and and_39 (and_39_out, or_18_out, Bit4_Shift[1]);
  and and_40 (and_40_out, ~Bit4_Shift[1], or_22_out);  // AND_Gate
  or or_19 (or_19_out, and_32_out, and_55_out);
  and and_41 (and_41_out, or_19_out, Bit4_Shift[2]);
  and and_42 (and_42_out, ~Bit4_Shift[2], or_23_out);  // AND_Gate
  or or_20 (or_20_out, and_34_out, and_73_out);
  and and_43 (and_43_out, or_20_out, Bit4_Shift[3]);
  and and_44 (and_44_out, ~Bit4_Shift[3], or_24_out);  // AND_Gate
  or or_21 (Bit16_Result[4], and_36_out, and_107_out);
  and and_45 (and_45_out, ~Bit4_Shift[0], Bit16_Data[6]);  // AND_Gate
  and and_46 (and_46_out, Bit16_Data[5], Bit4_Shift[0]);
  or or_22 (or_22_out, and_38_out, and_53_out);
  and and_47 (and_47_out, ~Bit4_Shift[1], or_26_out);  // AND_Gate
  and and_48 (and_48_out, or_22_out, Bit4_Shift[1]);
  or or_23 (or_23_out, and_40_out, and_63_out);
  and and_49 (and_49_out, ~Bit4_Shift[2], or_27_out);  // AND_Gate
  and and_50 (and_50_out, or_23_out, Bit4_Shift[2]);
  or or_24 (or_24_out, and_42_out, and_81_out);
  and and_51 (and_51_out, ~Bit4_Shift[3], or_28_out);  // AND_Gate
  and and_52 (and_52_out, or_24_out, Bit4_Shift[3]);
  or or_25 (Bit16_Result[5], and_44_out, and_115_out);
  and and_53 (and_53_out, Bit16_Data[6], Bit4_Shift[0]);
  and and_54 (and_54_out, ~Bit4_Shift[0], Bit16_Data[7]);  // AND_Gate
  or or_26 (or_26_out, and_45_out, and_61_out);
  and and_55 (and_55_out, or_26_out, Bit4_Shift[1]);
  and and_56 (and_56_out, ~Bit4_Shift[1], or_30_out);  // AND_Gate
  or or_27 (or_27_out, and_47_out, and_71_out);
  and and_57 (and_57_out, or_27_out, Bit4_Shift[2]);
  and and_58 (and_58_out, ~Bit4_Shift[2], or_31_out);  // AND_Gate
  or or_28 (or_28_out, and_49_out, and_89_out);
  and and_59 (and_59_out, or_28_out, Bit4_Shift[3]);
  and and_60 (and_60_out, ~Bit4_Shift[3], or_32_out);  // AND_Gate
  or or_29 (Bit16_Result[6], and_51_out, and_123_out);
  and and_61 (and_61_out, Bit16_Data[7], Bit4_Shift[0]);
  and and_62 (and_62_out, ~Bit4_Shift[0], Bit16_Data[8]);  // AND_Gate
  or or_30 (or_30_out, and_54_out, and_69_out);
  and and_63 (and_63_out, or_30_out, Bit4_Shift[1]);
  and and_64 (and_64_out, ~Bit4_Shift[1], or_34_out);  // AND_Gate
  or or_31 (or_31_out, and_56_out, and_79_out);
  and and_65 (and_65_out, or_31_out, Bit4_Shift[2]);
  and and_66 (and_66_out, ~Bit4_Shift[2], or_35_out);  // AND_Gate
  or or_32 (or_32_out, and_58_out, and_97_out);
  and and_67 (and_67_out, or_32_out, Bit4_Shift[3]);
  and and_68 (Bit16_Result[8], ~Bit4_Shift[3], or_36_out);  // AND_Gate
  or or_33 (Bit16_Result[7], and_60_out, and_128_out);
  and and_69 (and_69_out, Bit16_Data[8], Bit4_Shift[0]);
  and and_70 (and_70_out, ~Bit4_Shift[0], Bit16_Data[9]);  // AND_Gate
  or or_34 (or_34_out, and_62_out, and_77_out);
  and and_71 (and_71_out, or_34_out, Bit4_Shift[1]);
  and and_72 (and_72_out, ~Bit4_Shift[1], or_37_out);  // AND_Gate
  or or_35 (or_35_out, and_64_out, and_87_out);
  and and_73 (and_73_out, or_35_out, Bit4_Shift[2]);
  and and_74 (and_74_out, ~Bit4_Shift[2], or_38_out);  // AND_Gate
  or or_36 (or_36_out, and_66_out, and_105_out);
  and and_75 (and_75_out, or_36_out, Bit4_Shift[3]);
  and and_76 (Bit16_Result[9], ~Bit4_Shift[3], or_39_out);  // AND_Gate
  and and_77 (and_77_out, Bit16_Data[9], Bit4_Shift[0]);
  and and_78 (and_78_out, ~Bit4_Shift[0], Bit16_Data[10]);  // AND_Gate
  or or_37 (or_37_out, and_70_out, and_85_out);
  and and_79 (and_79_out, or_37_out, Bit4_Shift[1]);
  and and_80 (and_80_out, ~Bit4_Shift[1], or_40_out);  // AND_Gate
  or or_38 (or_38_out, and_72_out, and_95_out);
  and and_81 (and_81_out, or_38_out, Bit4_Shift[2]);
  and and_82 (and_82_out, ~Bit4_Shift[2], or_41_out);  // AND_Gate
  or or_39 (or_39_out, and_74_out, and_113_out);
  and and_83 (and_83_out, or_39_out, Bit4_Shift[3]);
  and and_84 (Bit16_Result[10], ~Bit4_Shift[3], or_42_out);  // AND_Gate
  and and_85 (and_85_out, Bit16_Data[10], Bit4_Shift[0]);
  and and_86 (and_86_out, ~Bit4_Shift[0], Bit16_Data[11]);  // AND_Gate
  or or_40 (or_40_out, and_78_out, and_93_out);
  and and_87 (and_87_out, or_40_out, Bit4_Shift[1]);
  and and_88 (and_88_out, ~Bit4_Shift[1], or_43_out);  // AND_Gate
  or or_41 (or_41_out, and_80_out, and_103_out);
  and and_89 (and_89_out, or_41_out, Bit4_Shift[2]);
  and and_90 (and_90_out, ~Bit4_Shift[2], or_44_out);  // AND_Gate
  or or_42 (or_42_out, and_82_out, and_121_out);
  and and_91 (and_91_out, or_42_out, Bit4_Shift[3]);
  and and_92 (Bit16_Result[11], ~Bit4_Shift[3], or_45_out);  // AND_Gate
  and and_93 (and_93_out, Bit16_Data[11], Bit4_Shift[0]);
  and and_94 (and_94_out, ~Bit4_Shift[0], Bit16_Data[12]);  // AND_Gate
  or or_43 (or_43_out, and_86_out, and_101_out);
  and and_95 (and_95_out, or_43_out, Bit4_Shift[1]);
  and and_96 (and_96_out, ~Bit4_Shift[1], or_46_out);  // AND_Gate
  or or_44 (or_44_out, and_88_out, and_111_out);
  and and_97 (and_97_out, or_44_out, Bit4_Shift[2]);
  and and_98 (and_98_out, ~Bit4_Shift[2], or_47_out);  // AND_Gate
  or or_45 (or_45_out, and_90_out, and_127_out);
  and and_99 (and_99_out, or_45_out, Bit4_Shift[3]);
  and and_100 (Bit16_Result[12], ~Bit4_Shift[3], and_98_out);  // AND_Gate
  and and_101 (and_101_out, Bit16_Data[12], Bit4_Shift[0]);
  and and_102 (and_102_out, ~Bit4_Shift[0], Bit16_Data[13]);  // AND_Gate
  or or_46 (or_46_out, and_94_out, and_109_out);
  and and_103 (and_103_out, or_46_out, Bit4_Shift[1]);
  and and_104 (and_104_out, ~Bit4_Shift[1], or_48_out);  // AND_Gate
  or or_47 (or_47_out, and_96_out, and_119_out);
  and and_105 (and_105_out, or_47_out, Bit4_Shift[2]);
  and and_106 (and_106_out, ~Bit4_Shift[2], or_49_out);  // AND_Gate
  and and_107 (and_107_out, and_98_out, Bit4_Shift[3]);
  and and_108 (Bit16_Result[13], ~Bit4_Shift[3], and_106_out);  // AND_Gate
  and and_109 (and_109_out, Bit16_Data[13], Bit4_Shift[0]);
  and and_110 (and_110_out, ~Bit4_Shift[0], Bit16_Data[14]);  // AND_Gate
  or or_48 (or_48_out, and_102_out, and_117_out);
  and and_111 (and_111_out, or_48_out, Bit4_Shift[1]);
  and and_112 (and_112_out, ~Bit4_Shift[1], or_50_out);  // AND_Gate
  or or_49 (or_49_out, and_104_out, and_126_out);
  and and_113 (and_113_out, or_49_out, Bit4_Shift[2]);
  and and_114 (and_114_out, ~Bit4_Shift[2], and_112_out);  // AND_Gate
  and and_115 (and_115_out, and_106_out, Bit4_Shift[3]);
  and and_116 (Bit16_Result[14], ~Bit4_Shift[3], and_114_out);  // AND_Gate
  and and_117 (and_117_out, Bit16_Data[14], Bit4_Shift[0]);
  and and_118 (and_118_out, ~Bit4_Shift[0], Bit16_Data[15]);  // AND_Gate
  or or_50 (or_50_out, and_110_out, and_125_out);
  and and_119 (and_119_out, or_50_out, Bit4_Shift[1]);
  and and_120 (and_120_out, ~Bit4_Shift[1], and_118_out);  // AND_Gate
  and and_121 (and_121_out, and_112_out, Bit4_Shift[2]);
  and and_122 (and_122_out, ~Bit4_Shift[2], and_120_out);  // AND_Gate
  and and_123 (and_123_out, and_114_out, Bit4_Shift[3]);
  and and_124 (Bit16_Result[15], ~Bit4_Shift[3], and_122_out);  // AND_Gate
  and and_125 (and_125_out, Bit16_Data[15], Bit4_Shift[0]);
  and and_126 (and_126_out, and_118_out, Bit4_Shift[1]);
  and and_127 (and_127_out, and_120_out, Bit4_Shift[2]);
  and and_128 (and_128_out, and_122_out, Bit4_Shift[3]);
endmodule

module Bit4_Controlled_Buffer (
  input  [3:0] Bit4_In,
  input  Enable,
  output [3:0] Bit4_Out
);

  and and_1 (Bit4_Out[0], Bit4_In[0], Enable);
  and and_2 (Bit4_Out[1], Bit4_In[1], Enable);
  and and_3 (Bit4_Out[2], Bit4_In[2], Enable);
  and and_4 (Bit4_Out[3], Bit4_In[3], Enable);
endmodule

module Bit4_Twos_Complementer (
  input  [3:0] Bit4_In,
  output [3:0] Bit4_Result
);

  wire or_1_out, or_2_out;

  or or_1 (or_1_out, Bit4_In[0], Bit4_Result[1]);
  or or_2 (or_2_out, Bit4_In[0], Bit4_Result[1], Bit4_Result[2]);
  xor xor_1 (Bit4_Result[1], Bit4_In[1], Bit4_In[0]);
  xor xor_2 (Bit4_Result[2], Bit4_In[2], or_1_out);
  xor xor_3 (Bit4_Result[3], Bit4_In[3], or_2_out);

  assign Bit4_Result[0] = Bit4_In[0];
endmodule

module Bit4_Adder (
  input  Cin,
  input  [3:0] Bit4_A,
  input  [3:0] Bit4_B,
  output Cout,
  output [3:0] Bit4_Result
);

  wire and_1_out, and_2_out, and_3_out, and_4_out, bit4_cla_logic_1_c2, bit4_cla_logic_1_c3,
       bit4_cla_logic_1_c4, xor_1_out, xor_2_out, xor_3_out, xor_4_out;

  xor xor_1 (xor_1_out, Bit4_A[0], Bit4_B[0]);
  and and_1 (and_1_out, Bit4_B[0], Bit4_A[0]);
  xor xor_2 (xor_2_out, Bit4_A[1], Bit4_B[1]);
  and and_2 (and_2_out, Bit4_B[1], Bit4_A[1]);
  xor xor_3 (xor_3_out, Bit4_A[2], Bit4_B[2]);
  and and_3 (and_3_out, Bit4_B[2], Bit4_A[2]);
  xor xor_4 (xor_4_out, Bit4_A[3], Bit4_B[3]);
  and and_4 (and_4_out, Bit4_B[3], Bit4_A[3]);
  xor xor_5 (Bit4_Result[3], xor_4_out, Cin);
  xor xor_6 (Bit4_Result[2], xor_3_out, bit4_cla_logic_1_c2);
  xor xor_7 (Bit4_Result[0], xor_1_out, bit4_cla_logic_1_c4);
  xor xor_8 (Bit4_Result[1], xor_2_out, bit4_cla_logic_1_c3);
  Bit4_CLA_Logic bit4_cla_logic_1 (
    .Cin(Cin), .P1(xor_1_out), .G1(and_1_out), .P2(xor_2_out), .G2(and_2_out), .P3(xor_3_out),
    .G3(and_3_out), .P4(xor_4_out), .G4(and_4_out), .C2(bit4_cla_logic_1_c2), .C3(bit4_cla_logic_1_c3),
    .C4(bit4_cla_logic_1_c4), .COUT(Cout));  // open: PG
endmodule

module Bit5_Adder (
  input  Cin,
  input  [4:0] Bit5_A,
  input  [4:0] Bit5_B,
  output [4:0] Bit5_Result,
  output Cout
);

  wire and_1_out, and_2_out, and_3_out, and_4_out, and_5_out, and_6_out, and_7_out, and_8_out, and_9_out,
       and_10_out, and_11_out, and_12_out, and_13_out, and_14_out, and_15_out, and_16_out, and_17_out,
       and_18_out, and_19_out, and_20_out, or_1_out, or_2_out, or_3_out, or_4_out, xor_1_out, xor_2_out,
       xor_3_out, xor_4_out, xor_5_out;

  xor xor_1 (xor_1_out, Bit5_B[3], Bit5_A[3]);
  and and_1 (and_1_out, Bit5_A[3], Bit5_B[3]);
  xor xor_2 (xor_2_out, Bit5_B[4], Bit5_A[4]);
  and and_2 (and_2_out, Bit5_A[4], Bit5_B[4]);
  xor xor_3 (xor_3_out, Bit5_B[0], Bit5_A[0]);
  and and_3 (and_3_out, Bit5_A[0], Bit5_B[0]);
  xor xor_4 (xor_4_out, Bit5_B[1], Bit5_A[1]);
  and and_4 (and_4_out, Bit5_A[1], Bit5_B[1]);
  xor xor_5 (xor_5_out, Bit5_B[2], Bit5_A[2]);
  and and_5 (and_5_out, Bit5_A[2], Bit5_B[2]);
  xor xor_6 (Bit5_Result[3], or_3_out, xor_1_out);
  xor xor_7 (Bit5_Result[4], or_4_out, xor_2_out);
  xor xor_8 (Bit5_Result[2], or_2_out, xor_5_out);
  xor xor_9 (Bit5_Result[0], Cin, xor_3_out);
  or or_1 (or_1_out, and_3_out, and_6_out);
  xor xor_10 (Bit5_Result[1], or_1_out, xor_4_out);
  or or_2 (or_2_out, and_4_out, and_7_out, and_8_out);
  or or_3 (or_3_out, and_5_out, and_9_out, and_10_out, and_11_out);
  or or_4 (or_4_out, and_1_out, and_12_out, and_13_out, and_14_out, and_15_out);
  or or_5 (Cout, and_2_out, and_16_out, and_17_out, and_18_out, and_19_out, and_20_out);
  and and_6 (and_6_out, xor_3_out, Cin);
  and and_7 (and_7_out, xor_4_out, and_3_out);
  and and_8 (and_8_out, xor_4_out, xor_3_out, Cin);
  and and_9 (and_9_out, and_4_out, xor_5_out);
  and and_10 (and_10_out, xor_5_out, xor_4_out, and_3_out);
  and and_11 (and_11_out, xor_5_out, xor_4_out, Cin, xor_3_out);
  and and_12 (and_12_out, and_5_out, xor_1_out);
  and and_13 (and_13_out, xor_1_out, xor_5_out, and_4_out);
  and and_14 (and_14_out, xor_1_out, xor_5_out, xor_4_out, and_3_out);
  and and_15 (and_15_out, xor_1_out, xor_5_out, xor_4_out, xor_3_out, Cin);
  and and_16 (and_16_out, xor_2_out, and_1_out);
  and and_17 (and_17_out, xor_2_out, xor_1_out, and_5_out);
  and and_18 (and_18_out, xor_2_out, xor_1_out, xor_5_out, and_4_out);
  and and_19 (and_19_out, xor_2_out, xor_1_out, xor_5_out, xor_4_out, and_3_out);
  and and_20 (and_20_out, xor_2_out, xor_1_out, xor_5_out, xor_4_out, xor_3_out, Cin);

  // Notes on the sheet:
  //   0
endmodule

module Bit5_Twos_Complementer (
  input  [4:0] Bit5_In,
  output [4:0] Bit5_Result
);

  wire or_1_out, or_2_out, or_3_out;

  or or_1 (or_1_out, Bit5_In[0], Bit5_Result[1]);
  or or_2 (or_2_out, Bit5_In[0], Bit5_Result[1], Bit5_Result[2]);
  or or_3 (or_3_out, Bit5_Result[3], Bit5_Result[1], Bit5_Result[2], Bit5_In[0]);
  xor xor_1 (Bit5_Result[1], Bit5_In[1], Bit5_In[0]);
  xor xor_2 (Bit5_Result[2], Bit5_In[2], or_1_out);
  xor xor_3 (Bit5_Result[3], Bit5_In[3], or_2_out);
  xor xor_4 (Bit5_Result[4], or_3_out, Bit5_In[4]);

  assign Bit5_Result[0] = Bit5_In[0];
endmodule
